// Logisim project Cache_hjc-owo.circ as structural Verilog: 10 circuits, main circuit Cache
module Cache (
  input  [31:0] Addr,
  input  [31:0] Data_in,
  input  MemWrite,
  input  clk,
  input  MemRead,
  input  reset,
  output [15:0] all,
  output [15:0] hit,
  output [31:0] Data_out,
  output stop
);

  wire and_1_out, and_2_out, and_7_out, and_8_out, Enable1, Enable2, Enable3, Enable4, Hit1, hit1_t, Hit2,
       hit2_t, Hit3, hit3_t, Hit4, hit4_t, hit_t, not_1_out, not_2_out, not_3_out, not_4_out, not_5_out,
       or_1_out, or_2_out, or_3_out, or_4_out;
  wire [1:0] or_6_out;
  wire [31:0] _1, _1_1, _1_2, _1_3, _1_4, _2, _2_1, _2_2, _2_3, _2_4, _3, _3_1, _3_2, _3_3, _3_4, _4, _4_1,
       _4_2, _4_3, _4_4, Data_out_Cache, Data_out_RAM, muxforgroup_1_out_18, muxforgroup_1_out_19,
       muxforgroup_1_out_20, muxforgroup_1_out_21;

  Decoder #(.select(2)) decoder_1 (.out0(Hit1), .out1(Hit2), .out2(Hit3), .out3(Hit4), .sel(Addr[5:4]));  // open: en
  not not_1 (not_1_out, stop);
  and and_1 (and_1_out, MemRead, not_1_out);
  Counter #(.width(16), .max('hffff)) counter_1 (
    .count(and_1_out), .Q(all), .clk(clk), .clr(reset));  // open: load, D, carry
  RAM ram_1 (
    .MuxBlock(Addr[3:2]), .MemWrite(MemWrite), .MemRead(MemRead), .Hit(hit_t), .Tag(Addr[11:6]),
    .MuxGroup(Addr[5:4]), .MemData(Data_in), .Clk(clk), .Reset(reset), ._4(_4), ._3(_3), ._2(_2),
    .out_13(stop), ._1(_1));
  not not_2 (not_2_out, stop);
  and and_2 (and_2_out, MemRead, hit_t, not_2_out);
  Counter #(.width(16), .max('hffff)) counter_2 (
    .count(and_2_out), .Q(hit), .clk(clk), .clr(reset));  // open: load, D, carry
  or or_1 (or_1_out, MemWrite, MemRead);
  or or_2 (or_2_out, MemWrite, MemRead);
  or or_3 (or_3_out, MemWrite, MemRead);
  or or_4 (or_4_out, MemWrite, MemRead);
  and and_3 (Enable1, Hit1, or_1_out);
  and and_4 (Enable2, Hit2, or_2_out);
  and and_5 (Enable3, Hit3, or_3_out);
  and and_6 (Enable4, Hit4, or_4_out);
  group group_1 (
    .in_1(clk), .in_2(reset), .in_3(stop), .in_4(Enable1), .in_5(MemRead), .in_6(MemWrite),
    .in_7(Addr[11:6]), .in_8(_1), .in_9(_2), .in_10(_3), .in_11(_4), .out_12(_1_1), .out_13(_1_2),
    .out_14(_1_3), .out_15(_1_4), .out_16(hit1_t));
  group group_2 (
    .in_1(clk), .in_2(reset), .in_3(stop), .in_4(Enable2), .in_5(MemRead), .in_6(MemWrite),
    .in_7(Addr[11:6]), .in_8(_1), .in_9(_2), .in_10(_3), .in_11(_4), .out_12(_2_1), .out_13(_2_2),
    .out_14(_2_3), .out_15(_2_4), .out_16(hit2_t));
  group group_3 (
    .in_1(clk), .in_2(reset), .in_3(stop), .in_4(Enable3), .in_5(MemRead), .in_6(MemWrite),
    .in_7(Addr[11:6]), .in_8(_1), .in_9(_2), .in_10(_3), .in_11(_4), .out_12(_3_1), .out_13(_3_2),
    .out_14(_3_3), .out_15(_3_4), .out_16(hit3_t));
  group group_4 (
    .in_1(clk), .in_2(reset), .in_3(stop), .in_4(Enable4), .in_5(MemRead), .in_6(MemWrite),
    .in_7(Addr[11:6]), .in_8(_1), .in_9(_2), .in_10(_3), .in_11(_4), .out_12(_4_1), .out_13(_4_2),
    .out_14(_4_3), .out_15(_4_4), .out_16(hit4_t));
  or or_5 (hit_t, hit1_t, hit2_t, hit3_t, hit4_t);
  and and_7 (and_7_out, stop, not_3_out);
  not not_3 (not_3_out, hit_t);
  not not_4 (not_4_out, stop);
  and and_8 (and_8_out, not_4_out, not_5_out);
  not not_5 (not_5_out, hit_t);
  MuxForGroup muxforgroup_1 (
    .in_1(_1_1), .in_2(_1_2), .in_3(_1_3), .in_4(_1_4), .in_5(_2_1), .in_6(_2_2), .in_7(_2_3), .in_8(_2_4),
    .in_9(_3_1), .in_10(_3_2), .in_11(_3_3), .in_12(_3_4), .in_13(_4_1), .in_14(_4_2), .in_15(_4_3),
    .in_16(_4_4), .out_18(muxforgroup_1_out_18), .in_17(Addr[5:4]), .out_19(muxforgroup_1_out_19),
    .out_20(muxforgroup_1_out_20), .out_21(muxforgroup_1_out_21));
  Multiplexer #(.select(2), .width(32)) multiplexer_1 (
    .in0(muxforgroup_1_out_18), .in1(muxforgroup_1_out_19), .in2(muxforgroup_1_out_20),
    .in3(muxforgroup_1_out_21), .out(Data_out_Cache), .sel(Addr[3:2]));  // open: en
  Multiplexer #(.select(2), .width(32)) multiplexer_2 (
    .in0(_1), .in1(_2), .in2(_3), .in3(_4), .out(Data_out_RAM), .sel(Addr[3:2]));  // open: en
  or or_6 (or_6_out[0], and_7_out, and_8_out, MemWrite);
  or or_7 (or_6_out[1], hit_t, MemWrite, and_7_out);
  Multiplexer #(.select(2), .width(32)) multiplexer_3 (
    .in1(Data_out_RAM), .in2(Data_out_Cache), .in3({32{1'b0}}), .out(Data_out), .sel(or_6_out));  // open: in0, en
  // Probe on or_6_out

  // Other names for the same wires on the sheet: MuxBlock[1:0] = Addr[3:2]; MuxGroup[1:0] = Addr[5:4];
  //   Tag[5:0] = Addr[11:6]
endmodule

module block (
  input  reset,
  input  clk,
  input  enable,
  input  [5:0] in_4,
  input  [31:0] in_5,
  input  [31:0] in_6,
  input  [31:0] in_7,
  input  [31:0] in_8,
  output out_9,
  output [5:0] out_10,
  output [31:0] out_11,
  output [31:0] out_12,
  output [31:0] out_13,
  output [31:0] out_14
);

  Register #(.width(1)) register_1 (.D(1'b1), .en(enable), .Q(out_9), .clk(clk), .clr(reset));
  Register #(.width(6)) register_2 (.D(in_4), .en(enable), .Q(out_10), .clk(clk), .clr(reset));
  Register #(.width(32)) register_3 (.D(in_5), .en(enable), .Q(out_11), .clk(clk), .clr(reset));
  Register #(.width(32)) register_4 (.D(in_6), .en(enable), .Q(out_12), .clk(clk), .clr(reset));
  Register #(.width(32)) register_5 (.D(in_7), .en(enable), .Q(out_13), .clk(clk), .clr(reset));
  Register #(.width(32)) register_6 (.D(in_8), .en(enable), .Q(out_14), .clk(clk), .clr(reset));
endmodule

module cmp (
  input  [2:0] in_1,
  input  [15:0] in_2,
  input  [2:0] in_3,
  input  [15:0] in_4,
  output [2:0] out_5,
  output [15:0] out_6
);

  wire comparator_1_eq, comparator_1_gt, or_1_out;

  Comparator #(.width(19), .mode("unsigned")) comparator_1 (
    .a({in_2, in_1}), .b({in_4, in_3}), .gt(comparator_1_gt), .eq(comparator_1_eq));  // open: lt
  or or_1 (or_1_out, comparator_1_gt, comparator_1_eq);
  Multiplexer #(.width(19)) multiplexer_1 (
    .in0({in_4, in_3}), .in1({in_2, in_1}), .out({out_6, out_5}), .sel(or_1_out));  // open: en
endmodule

module LRU (
  input  [15:0] in_1,
  input  [15:0] in_2,
  input  [15:0] in_3,
  input  [15:0] in_4,
  input  in_5,
  input  in_6,
  input  in_7,
  input  in_8,
  input  in_9,
  input  in_10,
  input  in_11,
  output out_12,
  output out_13,
  output out_14,
  output out_15
);

  wire comparator_1_eq, comparator_2_eq, comparator_3_eq, comparator_4_eq, get, multiplexer_1_out,
       multiplexer_2_out, multiplexer_3_out, multiplexer_4_out, not_1_out, not_2_out, not_3_out, not_4_out,
       not_5_out, not_6_out, not_7_out, not_8_out;
  wire [1:0] and_1_out, and_3_out, and_5_out, and_7_out;
  wire [2:0] cmp_1_out_5, cmp_2_out_5, cmp_3_out_5, subtractor_1_out;
  wire [15:0] cmp_1_out_6, cmp_2_out_6;

  or or_1 (get, in_8, in_7, in_6, in_5);
  cmp cmp_1 (.in_1(3'b011), .in_2(in_1), .in_3(3'b010), .in_4(in_2), .out_5(cmp_1_out_5), .out_6(cmp_1_out_6));
  cmp cmp_2 (.in_1(3'b001), .in_2(in_3), .in_3(3'b000), .in_4(in_4), .out_5(cmp_2_out_5), .out_6(cmp_2_out_6));
  cmp cmp_3 (
    .in_1(cmp_1_out_5), .in_2(cmp_1_out_6), .in_3(cmp_2_out_5), .in_4(cmp_2_out_6), .out_5(cmp_3_out_5));  // open: out_6
  Subtractor #(.width(3)) subtractor_1 (.a(3'b100), .b(cmp_3_out_5), .out(subtractor_1_out));  // open: bin, bout
  Comparator #(.width(3)) comparator_1 (.a(subtractor_1_out), .b(3'b001), .eq(comparator_1_eq));  // open: gt, lt
  Comparator #(.width(3)) comparator_2 (.a(subtractor_1_out), .b(3'b010), .eq(comparator_2_eq));  // open: gt, lt
  Comparator #(.width(3)) comparator_3 (.a(subtractor_1_out), .b(3'b011), .eq(comparator_3_eq));  // open: gt, lt
  Comparator #(.width(3)) comparator_4 (.a(subtractor_1_out), .b(3'b100), .eq(comparator_4_eq));  // open: gt, lt
  not not_1 (not_1_out, get);
  not not_2 (not_2_out, in_10);
  not not_3 (not_3_out, get);
  not not_4 (not_4_out, in_10);
  not not_5 (not_5_out, get);
  not not_6 (not_6_out, in_10);
  not not_7 (not_7_out, get);
  not not_8 (not_8_out, in_10);
  and and_1 (and_1_out[0], in_5, in_10);
  and and_2 (and_1_out[1], not_1_out, not_2_out);
  and and_3 (and_3_out[0], in_6, in_10);
  and and_4 (and_3_out[1], not_3_out, not_4_out);
  and and_5 (and_5_out[0], in_7, in_10);
  and and_6 (and_5_out[1], not_5_out, not_6_out);
  and and_7 (and_7_out[0], in_8, in_10);
  and and_8 (and_7_out[1], not_7_out, not_8_out);
  Multiplexer #(.select(2)) multiplexer_1 (
    .in0(1'b0), .in1(1'b1), .in2(comparator_1_eq), .out(multiplexer_1_out), .sel(and_1_out));  // open: in3, en
  Multiplexer #(.select(2)) multiplexer_2 (
    .in0(1'b0), .in1(1'b1), .in2(comparator_2_eq), .out(multiplexer_2_out), .sel(and_3_out));  // open: in3, en
  Multiplexer #(.select(2)) multiplexer_3 (
    .in0(1'b0), .in1(1'b1), .in2(comparator_3_eq), .out(multiplexer_3_out), .sel(and_5_out));  // open: in3, en
  Multiplexer #(.select(2)) multiplexer_4 (
    .in0(1'b0), .in1(1'b1), .in2(comparator_4_eq), .out(multiplexer_4_out), .sel(and_7_out));  // open: in3, en
  and and_9 (out_12, multiplexer_1_out, in_11);
  and and_10 (out_13, multiplexer_2_out, in_11);
  and and_11 (out_14, multiplexer_3_out, in_11);
  and and_12 (out_15, multiplexer_4_out, in_11);

  // Other names for the same wires on the sheet: _1 = in_5; _2 = in_6; _3 = in_7; _4 = in_8; enable = in_11;
  //   MemRead = in_9; MemWrite = in_10
endmodule

module RAM (
  input  [1:0] MuxBlock,
  input  MemWrite,
  input  MemRead,
  input  Hit,
  input  [5:0] Tag,
  input  [1:0] MuxGroup,
  input  [31:0] MemData,
  input  Clk,
  input  Reset,
  output [31:0] _4,
  output [31:0] _3,
  output [31:0] _2,
  output out_13,
  output [31:0] _1
);

  wire _1_t, _2_t, _3_t, _4_t, and_1_out, and_2_out, counter_1_carry, not_1_out, not_2_out;
  wire [9:0] adder_1_out, adder_2_out, adder_3_out, adder_4_out, multiplexer_1_out;
  wire [31:0] ram_1_data, ram_2_data, ram_3_data, ram_4_data;

  and and_1 (and_1_out, MemRead, not_1_out);
  not not_1 (not_1_out, Hit);
  Counter #(.width(3), .max('h5)) counter_1 (
    .count(and_1_out), .carry(counter_1_carry), .clk(Clk), .clr(Reset));  // open: load, D, Q
  and and_2 (and_2_out, MemRead, Hit);
  and and_3 (out_13, and_1_out, not_2_out);
  not not_2 (not_2_out, counter_1_carry);
  Demultiplexer #(.select(2)) demultiplexer_1 (
    .out0(_1_t), .out1(_2_t), .out2(_3_t), .out3(_4_t), .in(MemWrite), .sel(MuxBlock));  // open: en
  Multiplexer #(.width(10), .enable("false")) multiplexer_1 (
    .in0({Tag, MuxGroup, 2'b00}), .in1({10{1'b0}}), .out(multiplexer_1_out), .sel(and_2_out));
  Adder #(.width(10)) adder_1 (.a(10'h3), .b(multiplexer_1_out), .out(adder_1_out));  // open: cin, cout
  Adder #(.width(10)) adder_2 (.a(10'h2), .b(multiplexer_1_out), .out(adder_2_out));  // open: cin, cout
  Adder #(.width(10)) adder_3 (.a(10'h1), .b(multiplexer_1_out), .out(adder_3_out));  // open: cin, cout
  Adder #(.width(10)) adder_4 (.a({10{1'b0}}), .b(multiplexer_1_out), .out(adder_4_out));  // open: cin, cout
  RAM_part #(.addrWidth(10), .dataWidth(32), .bus("separate")) ram_1 (
    .addr(adder_1_out), .din(MemData), .data(ram_1_data), .str(_4_t), .clk(Clk), .clr(Reset));  // open: sel, ld
  RAM_part #(.addrWidth(10), .dataWidth(32), .bus("separate")) ram_2 (
    .addr(adder_2_out), .din(MemData), .data(ram_2_data), .str(_3_t), .clk(Clk), .clr(Reset));  // open: sel, ld
  RAM_part #(.addrWidth(10), .dataWidth(32), .bus("separate")) ram_3 (
    .addr(adder_3_out), .din(MemData), .data(ram_3_data), .str(_2_t), .clk(Clk), .clr(Reset));  // open: sel, ld
  RAM_part #(.addrWidth(10), .dataWidth(32), .bus("separate")) ram_4 (
    .addr(adder_4_out), .din(MemData), .data(ram_4_data), .str(_1_t), .clk(Clk), .clr(Reset));  // open: sel, ld
  Multiplexer #(.width(32), .enable("false")) multiplexer_2 (.in0(ram_1_data), .in1(MemData), .out(_4), .sel(_4_t));
  Multiplexer #(.width(32), .enable("false")) multiplexer_3 (.in0(ram_2_data), .in1(MemData), .out(_3), .sel(_3_t));
  Multiplexer #(.width(32), .enable("false")) multiplexer_4 (.in0(ram_3_data), .in1(MemData), .out(_2), .sel(_2_t));
  Multiplexer #(.width(32), .enable("false")) multiplexer_5 (.in0(ram_4_data), .in1(MemData), .out(_1), .sel(_1_t));

  // Other names for the same wires on the sheet: Data[31:0] = MemData
endmodule

module counter (
  input  in_1,
  input  in_2,
  input  in_3,
  input  in_4,
  input  in_5,
  input  in_6,
  output [15:0] out_7
);

  wire and_1_out, and_2_out, and_3_out, and_4_out, load0, not_1_out, not_2_out;

  not not_1 (not_1_out, in_3);
  and and_1 (and_1_out, in_2, in_3);
  and and_2 (and_2_out, not_1_out, in_2, in_4);
  and and_3 (and_3_out, in_6, load0);
  not not_2 (not_2_out, load0);
  and and_4 (and_4_out, not_2_out, in_6, in_2);
  or or_1 (load0, and_1_out, and_2_out);
  Counter #(.width(16), .max('hffff)) counter_1 (
    .load(and_3_out), .D({16{1'b0}}), .count(and_4_out), .Q(out_7), .clk(in_1), .clr(in_5));  // open: carry

  // Other names for the same wires on the sheet: clk = in_1; enable = in_4; GroupEnable = in_6; hit = in_3;
  //   MemRead = in_2; reset = in_5
endmodule

module MuxForBlock (
  input  [31:0] in_1,
  input  [31:0] in_2,
  input  [31:0] in_3,
  input  [31:0] in_4,
  input  [31:0] in_5,
  input  [31:0] in_6,
  input  [31:0] in_7,
  input  [31:0] in_8,
  input  [31:0] in_9,
  input  [31:0] in_10,
  input  [31:0] in_11,
  input  [31:0] in_12,
  input  [31:0] in_13,
  input  [31:0] in_14,
  input  [31:0] in_15,
  input  [31:0] in_16,
  input  in_17,
  input  in_18,
  input  in_19,
  input  in_20,
  output [31:0] out_21,
  output [31:0] out_22,
  output [31:0] out_23,
  output [31:0] out_24
);

  Multiplexer #(.select(4), .width(32)) multiplexer_1 (
    .in0({32{1'b0}}), .in1(in_1), .in2(in_5), .in4(in_9), .in8(in_13), .out(out_21),
    .sel({in_20, in_19, in_18, in_17}));  // open: in3, in5, in6, in7, in9, in10, in11, in12, in13, in14, in15, en
  Multiplexer #(.select(4), .width(32)) multiplexer_2 (
    .in0({32{1'b0}}), .in1(in_2), .in2(in_6), .in4(in_10), .in8(in_14), .out(out_22),
    .sel({in_20, in_19, in_18, in_17}));  // open: in3, in5, in6, in7, in9, in10, in11, in12, in13, in14, in15, en
  Multiplexer #(.select(4), .width(32)) multiplexer_3 (
    .in0({32{1'b0}}), .in1(in_3), .in2(in_7), .in4(in_11), .in8(in_15), .out(out_23),
    .sel({in_20, in_19, in_18, in_17}));  // open: in3, in5, in6, in7, in9, in10, in11, in12, in13, in14, in15, en
  Multiplexer #(.select(4), .width(32)) multiplexer_4 (
    .in0({32{1'b0}}), .in1(in_4), .in2(in_8), .in4(in_12), .in8(in_16), .out(out_24),
    .sel({in_20, in_19, in_18, in_17}));  // open: in3, in5, in6, in7, in9, in10, in11, in12, in13, in14, in15, en

  // Other names for the same wires on the sheet: _1_1[31:0] = in_1; _1_2[31:0] = in_2; _1_3[31:0] = in_3;
  //   _1_4[31:0] = in_4; _2_1[31:0] = in_5; _2_2[31:0] = in_6; _2_3[31:0] = in_7; _2_4[31:0] = in_8;
  //   _3_1[31:0] = in_9; _3_2[31:0] = in_10; _3_3[31:0] = in_11; _3_4[31:0] = in_12; _4_1[31:0] = in_13;
  //   _4_2[31:0] = in_14; _4_3[31:0] = in_15; _4_4[31:0] = in_16; select[3:0] = {in_20, in_19, in_18, in_17}
endmodule

module group (
  input  in_1,
  input  in_2,
  input  in_3,
  input  in_4,
  input  in_5,
  input  in_6,
  input  [5:0] in_7,
  input  [31:0] in_8,
  input  [31:0] in_9,
  input  [31:0] in_10,
  input  [31:0] in_11,
  output [31:0] out_12,
  output [31:0] out_13,
  output [31:0] out_14,
  output [31:0] out_15,
  output out_16
);

  wire comparator_1_eq, comparator_2_eq, comparator_3_eq, comparator_4_eq, Enable, enable1, enable2, enable3,
       enable4, hit1, hit2, hit3, hit4, not_1_out, or_1_out, v1, v2, v3, v4;
  wire [5:0] Tag1, Tag2, Tag3, Tag4;
  wire [15:0] cnt1, cnt2, cnt3, cnt4;
  wire [31:0] _1_1, _1_2, _1_3, _1_4, _2_1, _2_2, _2_3, _2_4, _3_1, _3_2, _3_3, _3_4, _4_1, _4_2, _4_3, _4_4;

  not not_1 (not_1_out, in_3);
  and and_1 (Enable, not_1_out, in_4);
  Comparator #(.width(6)) comparator_1 (.a(Tag1), .b(in_7), .eq(comparator_1_eq));  // open: gt, lt
  Comparator #(.width(6)) comparator_2 (.a(Tag2), .b(in_7), .eq(comparator_2_eq));  // open: gt, lt
  Comparator #(.width(6)) comparator_3 (.a(Tag3), .b(in_7), .eq(comparator_3_eq));  // open: gt, lt
  Comparator #(.width(6)) comparator_4 (.a(Tag4), .b(in_7), .eq(comparator_4_eq));  // open: gt, lt
  and and_2 (hit1, v1, comparator_1_eq);
  and and_3 (hit2, v2, comparator_2_eq);
  and and_4 (hit3, v3, comparator_3_eq);
  and and_5 (hit4, v4, comparator_4_eq);
  LRU lru_1 (
    .in_1(cnt1), .in_2(cnt2), .in_3(cnt3), .in_4(cnt4), .in_5(hit1), .in_6(hit2), .in_7(hit3), .in_8(hit4),
    .in_9(in_5), .in_10(in_6), .in_11(Enable), .out_12(enable1), .out_13(enable2), .out_14(enable3),
    .out_15(enable4));
  block block_1 (
    .reset(in_2), .clk(in_1), .enable(enable1), .in_4(in_7), .in_5(in_8), .in_6(in_9), .in_7(in_10),
    .in_8(in_11), .out_9(v1), .out_10(Tag1), .out_11(_1_1), .out_12(_1_2), .out_13(_1_3), .out_14(_1_4));
  block block_2 (
    .reset(in_2), .clk(in_1), .enable(enable2), .in_4(in_7), .in_5(in_8), .in_6(in_9), .in_7(in_10),
    .in_8(in_11), .out_9(v2), .out_10(Tag2), .out_11(_2_1), .out_12(_2_2), .out_13(_2_3), .out_14(_2_4));
  block block_3 (
    .reset(in_2), .clk(in_1), .enable(enable3), .in_4(in_7), .in_5(in_8), .in_6(in_9), .in_7(in_10),
    .in_8(in_11), .out_9(v3), .out_10(Tag3), .out_11(_3_1), .out_12(_3_2), .out_13(_3_3), .out_14(_3_4));
  block block_4 (
    .reset(in_2), .clk(in_1), .enable(enable4), .in_4(in_7), .in_5(in_8), .in_6(in_9), .in_7(in_10),
    .in_8(in_11), .out_9(v4), .out_10(Tag4), .out_11(_4_1), .out_12(_4_2), .out_13(_4_3), .out_14(_4_4));
  counter counter_1 (.in_1(in_1), .in_2(in_5), .in_3(hit1), .in_4(enable1), .in_5(in_2), .out_7(cnt1), .in_6(Enable));
  counter counter_2 (.in_1(in_1), .in_2(in_5), .in_3(hit2), .in_4(enable2), .in_5(in_2), .out_7(cnt2), .in_6(Enable));
  counter counter_3 (.in_1(in_1), .in_2(in_5), .in_3(hit3), .in_4(enable3), .in_5(in_2), .out_7(cnt3), .in_6(Enable));
  counter counter_4 (.in_1(in_1), .in_2(in_5), .in_3(hit4), .in_4(enable4), .in_5(in_2), .out_7(cnt4), .in_6(Enable));
  or or_1 (or_1_out, hit1, hit2, hit3, hit4);
  MuxForBlock muxforblock_1 (
    .in_1(_1_1), .in_2(_1_2), .in_3(_1_3), .in_4(_1_4), .in_5(_2_1), .in_6(_2_2), .in_7(_2_3), .in_8(_2_4),
    .in_9(_3_1), .in_10(_3_2), .in_11(_3_3), .in_12(_3_4), .in_13(_4_1), .in_14(_4_2), .in_15(_4_3),
    .in_16(_4_4), .in_17(hit1), .in_18(hit2), .in_19(hit3), .in_20(hit4), .out_21(out_12), .out_22(out_13),
    .out_23(out_14), .out_24(out_15));
  and and_6 (out_16, or_1_out, in_4);

  // Other names for the same wires on the sheet: _1[31:0] = out_12; _2[31:0] = out_13; _3[31:0] = out_14;
  //   _4[31:0] = out_15; clk = in_1; enable_t = in_4; hit = out_16; in1[31:0] = in_8; in2[31:0] = in_9;
  //   in3[31:0] = in_10; in4[31:0] = in_11; MemRead = in_5; MemWrite = in_6; reset = in_2; stop = in_3;
  //   Tag[5:0] = in_7
endmodule

module MuxForGroup (
  input  [31:0] in_1,
  input  [31:0] in_2,
  input  [31:0] in_3,
  input  [31:0] in_4,
  input  [31:0] in_5,
  input  [31:0] in_6,
  input  [31:0] in_7,
  input  [31:0] in_8,
  input  [31:0] in_9,
  input  [31:0] in_10,
  input  [31:0] in_11,
  input  [31:0] in_12,
  input  [31:0] in_13,
  input  [31:0] in_14,
  input  [31:0] in_15,
  input  [31:0] in_16,
  input  [1:0] in_17,
  output [31:0] out_18,
  output [31:0] out_19,
  output [31:0] out_20,
  output [31:0] out_21
);

  Multiplexer #(.select(2), .width(32)) multiplexer_1 (
    .in0(in_1), .in1(in_5), .in2(in_9), .in3(in_13), .out(out_18), .sel(in_17));  // open: en
  Multiplexer #(.select(2), .width(32)) multiplexer_2 (
    .in0(in_2), .in1(in_6), .in2(in_10), .in3(in_14), .out(out_19), .sel(in_17));  // open: en
  Multiplexer #(.select(2), .width(32)) multiplexer_3 (
    .in0(in_3), .in1(in_7), .in2(in_11), .in3(in_15), .out(out_20), .sel(in_17));  // open: en
  Multiplexer #(.select(2), .width(32)) multiplexer_4 (
    .in0(in_4), .in1(in_8), .in2(in_12), .in3(in_16), .out(out_21), .sel(in_17));  // open: en

  // Other names for the same wires on the sheet: _1_1[31:0] = in_1; _1_2[31:0] = in_2; _1_3[31:0] = in_3;
  //   _1_4[31:0] = in_4; _2_1[31:0] = in_5; _2_2[31:0] = in_6; _2_3[31:0] = in_7; _2_4[31:0] = in_8;
  //   _3_1[31:0] = in_9; _3_2[31:0] = in_10; _3_3[31:0] = in_11; _3_4[31:0] = in_12; _4_1[31:0] = in_13;
  //   _4_2[31:0] = in_14; _4_3[31:0] = in_15; _4_4[31:0] = in_16; select[1:0] = in_17
endmodule

module counter_FIFO (
  input  in_1,
  input  in_2,
  input  in_3,
  input  in_4,
  input  in_5,
  input  in_6,
  output [15:0] out_7
);

  wire and_1_out, and_2_out, and_3_out, and_4_out, load0, not_1_out, not_2_out;

  not not_1 (not_1_out, in_3);
  and and_1 (and_1_out, in_2, in_3);
  and and_2 (and_2_out, not_1_out, in_2, in_4);
  and and_3 (and_3_out, in_6, load0);
  and and_4 (and_4_out, in_6, not_2_out);
  not not_2 (not_2_out, load0);
  or or_1 (load0, and_1_out, and_2_out);
  Counter #(.width(16), .max('hffff)) counter_1 (
    .load(and_3_out), .D({16{1'b0}}), .count(and_4_out), .Q(out_7), .clk(in_1), .clr(in_5));  // open: carry

  // Other names for the same wires on the sheet: clk = in_1; enable = in_4; GroupEnable = in_6; hit = in_3;
  //   MemRead = in_2; reset = in_5
endmodule
