// Logisim project LRU.circ as structural Verilog: 2 circuits, main circuit LRU
module LRU (
  input  [15:0] in_1,
  input  [15:0] in_2,
  input  [15:0] in_3,
  input  [15:0] in_4,
  input  in_5,
  input  in_6,
  input  in_7,
  input  in_8,
  input  in_9,
  input  in_10,
  input  in_11,
  output out_12,
  output out_13,
  output out_14,
  output out_15
);

  wire cmp_2_p3, cmp_2_p4, comparator_1_eq, comparator_2_eq, comparator_3_eq, comparator_4_eq, get,
       multiplexer_1_out, multiplexer_2_out, multiplexer_3_out, multiplexer_4_out, not_1_out, not_2_out,
       not_3_out, not_4_out, not_5_out, not_6_out, not_7_out, not_8_out;
  wire [1:0] and_1_out, and_3_out, and_5_out, and_7_out;
  wire [2:0] cmp_1_p3, cmp_3_out_5, subtractor_1_out;
  wire [15:0] cmp_1_p4;

  or or_1 (get, in_8, in_7, in_6, in_5);
  // cmp cmp_1: pin names not known; wires that end beside it: 3'b011, in_1, cmp_1_p3, cmp_1_p4
  // cmp cmp_2: pin names not known; wires that end beside it: 3'b001, in_3, cmp_2_p3, cmp_2_p4
  cmp cmp_3 (.in_1(cmp_1_p3), .in_4(cmp_1_p4), .out_5(cmp_3_out_5));  // open: in_2, in_3, out_6
  Subtractor #(.width(3)) subtractor_1 (.a(3'b100), .b(cmp_3_out_5), .out(subtractor_1_out));  // open: bin, bout
  Comparator #(.width(3)) comparator_1 (.a(subtractor_1_out), .b(3'b001), .eq(comparator_1_eq));  // open: gt, lt
  Comparator #(.width(3)) comparator_2 (.a(subtractor_1_out), .b(3'b010), .eq(comparator_2_eq));  // open: gt, lt
  Comparator #(.width(3)) comparator_3 (.a(subtractor_1_out), .b(3'b011), .eq(comparator_3_eq));  // open: gt, lt
  Comparator #(.width(3)) comparator_4 (.a(subtractor_1_out), .b(3'b100), .eq(comparator_4_eq));  // open: gt, lt
  not not_1 (not_1_out, get);
  not not_2 (not_2_out, in_10);
  not not_3 (not_3_out, get);
  not not_4 (not_4_out, in_10);
  not not_5 (not_5_out, get);
  not not_6 (not_6_out, in_10);
  not not_7 (not_7_out, get);
  not not_8 (not_8_out, in_10);
  and and_1 (and_1_out[0], in_5, in_10);
  and and_2 (and_1_out[1], not_1_out, not_2_out);
  and and_3 (and_3_out[0], in_6, in_10);
  and and_4 (and_3_out[1], not_3_out, not_4_out);
  and and_5 (and_5_out[0], in_7, in_10);
  and and_6 (and_5_out[1], not_5_out, not_6_out);
  and and_7 (and_7_out[0], in_8, in_10);
  and and_8 (and_7_out[1], not_7_out, not_8_out);
  Multiplexer #(.select(2)) multiplexer_1 (
    .in0(1'b0), .in1(1'b1), .in2(comparator_1_eq), .out(multiplexer_1_out), .sel(and_1_out));  // open: in3, en
  Multiplexer #(.select(2)) multiplexer_2 (
    .in0(1'b0), .in1(1'b1), .in2(comparator_2_eq), .out(multiplexer_2_out), .sel(and_3_out));  // open: in3, en
  Multiplexer #(.select(2)) multiplexer_3 (
    .in0(1'b0), .in1(1'b1), .in2(comparator_3_eq), .out(multiplexer_3_out), .sel(and_5_out));  // open: in3, en
  Multiplexer #(.select(2)) multiplexer_4 (
    .in0(1'b0), .in1(1'b1), .in2(comparator_4_eq), .out(multiplexer_4_out), .sel(and_7_out));  // open: in3, en
  and and_9 (out_12, multiplexer_1_out, in_11);
  and and_10 (out_13, multiplexer_2_out, in_11);
  and and_11 (out_14, multiplexer_3_out, in_11);
  and and_12 (out_15, multiplexer_4_out, in_11);

  // Other names for the same wires on the sheet: _1 = in_5; _2 = in_6; _3 = in_7; _4 = in_8; enable = in_11;
  //   MemRead = in_9; MemWrite = in_10
endmodule

module cmp (
  input  [2:0] in_1,
  input  [15:0] in_2,
  input  [2:0] in_3,
  input  [15:0] in_4,
  output [2:0] out_5,
  output [15:0] out_6
);

  wire comparator_1_eq, comparator_1_gt, or_1_out;

  Comparator #(.width(19), .mode("unsigned")) comparator_1 (
    .a({in_2, in_1}), .b({in_4, in_3}), .gt(comparator_1_gt), .eq(comparator_1_eq));  // open: lt
  or or_1 (or_1_out, comparator_1_gt, comparator_1_eq);
  Multiplexer #(.width(19)) multiplexer_1 (
    .in0({in_4, in_3}), .in1({in_2, in_1}), .out({out_6, out_5}), .sel(or_1_out));  // open: en
endmodule
