// Logisim project exam3.circ as structural Verilog: 1 circuit, main circuit fence
module fence (
  input  [7:0] in_1,
  input  [3:0] in_2,
  output [7:0] out_3
);

  wire and_1_out, and_2_out, and_3_out, and_4_out, and_5_out, and_6_out, and_7_out, and_8_out, and_9_out,
       and_10_out, and_11_out, and_12_out;

  and and_1 (and_1_out, in_1[5], in_2[1]);
  or or_1 (out_3[6], and_1_out, and_2_out);
  and and_2 (and_2_out, in_1[3], in_2[2]);
  and and_3 (and_3_out, in_1[3], in_2[1]);
  or or_2 (out_3[5], and_3_out, and_4_out);
  and and_4 (and_4_out, in_1[6], in_2[2]);
  and and_5 (and_5_out, in_1[1], in_2[1]);
  or or_3 (out_3[4], and_5_out, and_6_out);
  and and_6 (and_6_out, in_1[2], in_2[2]);
  and and_7 (and_7_out, in_1[6], in_2[1]);
  or or_4 (out_3[3], and_7_out, and_8_out);
  and and_8 (and_8_out, in_1[5], in_2[2]);
  and and_9 (and_9_out, in_1[4], in_2[1]);
  or or_5 (out_3[2], and_9_out, and_10_out);
  and and_10 (and_10_out, in_1[1], in_2[2]);
  and and_11 (and_11_out, in_1[2], in_2[1]);
  or or_6 (out_3[1], and_11_out, and_12_out);
  and and_12 (and_12_out, in_1[4], in_2[2]);

  assign {out_3[7], out_3[0]} = {in_1[7], in_1[0]};
endmodule
