// Logisim project pipeline_cpu_hjc-owo.circ as structural Verilog: 21 circuits, main circuit main
module main (
  input  in_1,
  output [31:0] out_2,
  output out_3,
  output [4:0] out_4,
  output [31:0] out_5,
  output out_6,
  output [4:0] out_7,
  output [31:0] out_8
);

  wire ALUSrc, Clk, comparator_1_eq, control_1_beq, control_1_j_jal, control_1_jr, d_e_reg_1_alusrc_o,
       d_e_reg_1_memread_o, d_e_reg_1_memwrite_o, d_e_reg_1_regwrite_o, e_m_reg_1_memread_o,
       e_m_reg_1_memwrite_o, e_m_reg_1_regwrite_o, flushE, forwardunit_1_frtmsel, MemRead, MemWrite, NPC,
       RegWrite, stallD, stallF;
  wire [1:0] d_1_tuse1_d, d_1_tuse2_d, d_e_reg_1_memtoreg_o, d_e_reg_1_regdst_o, e_m_reg_1_memtoreg_o,
       ext_op, forwardunit_1_frsdsel, forwardunit_1_frsesel, forwardunit_1_frtdsel, forwardunit_1_frtesel,
       m_w_reg_1_out_27, MemToReg, NPCop, RegDst;
  wire [3:0] ALUop, d_e_reg_1_aluop_o, e_1_tnew_e, m_1_tnew_m, w_1_tnew_w;
  wire [4:0] d_1_s1_d, d_1_s2_d, d_e_reg_1_rd_o, d_e_reg_1_rt_o, e_1_des_e, e_1_s1_e, e_1_s2_e,
       e_m_reg_1_out_20, instr_1_rd, instr_1_rs, instr_1_rt, m_1_des_m, m_1_s2_m, multiplexer_2_out,
       w_1_des_w;
  wire [5:0] instr_1_func, instr_1_op;
  wire [15:0] instr_1_imm16;
  wire [23:0] pc_1_instraddr;
  wire [25:0] Jtarget26;
  wire [31:0] adder_1_out, adder_2_out, alu_1_out_4, ALUresult_W, d_e_reg_1_imm32_2, d_e_reg_1_out_29,
       d_e_reg_1_pc_4_o, d_e_reg_1_pc_8_o, d_e_reg_1_pc_o, dm_1_out_7, E__D, e_m_reg_1_out_18,
       e_m_reg_1_out_24, e_m_reg_1_pc_4_o, e_m_reg_1_pc_8_o, e_m_reg_1_pc_o, f_d_reg_1_instr_o,
       f_d_reg_1_pc_4_o, f_d_reg_1_pc_8_o, f_d_reg_1_pc_o, Fwd_ALU_A_E, Fwd_ALU_B_E, Fwd_RD1_D, Fwd_RD2_D,
       Fwd_WD_M, imm32, M__D, MemAddr_W, multiplexer_1_out, multiplexer_3_out, npc_2_npc, pc_1_pc, pc_8_W,
       RD1, RD1_E, RD2, RD2_E, readData_W, rom_1_data, W__D, WD_M;

  // Probe on multiplexer_1_out
  Clock clock_1 (.out(Clk));
  PC pc_1 (.in_2(in_1), .in_1(Clk), .NPC(multiplexer_1_out), .PC(pc_1_pc), .stallF(stallF), .InstrAddr(pc_1_instraddr));
  Multiplexer #(.width(32), .enable("false")) multiplexer_1 (
    .in0(adder_1_out), .in1(npc_2_npc), .out(multiplexer_1_out), .sel(NPC));
  Adder #(.width(32)) adder_1 (.a(pc_1_pc), .b(32'h4), .out(adder_1_out));  // open: cin, cout
  Adder #(.width(32)) adder_2 (.a(pc_1_pc), .b(32'h8), .out(adder_2_out));  // open: cin, cout
  ROM #(.addrWidth(24), .dataWidth(32)) rom_1 (.addr(pc_1_instraddr), .data(rom_1_data));  // open: sel
  F_D_reg f_d_reg_1 (
    .instr_i(rom_1_data), .pc_i(pc_1_pc), .instr_o(f_d_reg_1_instr_o), .pc_o(f_d_reg_1_pc_o), .in_1(Clk),
    .in_2(in_1), .in_7(stallD), .pc_4_o(f_d_reg_1_pc_4_o), .pc_8_o(f_d_reg_1_pc_8_o), .pc_4_i(adder_1_out),
    .pc_8_i(adder_2_out));
  Instr instr_1 (
    .Instr(f_d_reg_1_instr_o), .func(instr_1_func), .Rs(instr_1_rs), .Rt(instr_1_rt), .Rd(instr_1_rd),
    .Op(instr_1_op), .imm16(instr_1_imm16), .Jtarget26(Jtarget26));
  // Probe on f_d_reg_1_pc_4_o
  control control_1 (
    .ALUSrc(ALUSrc), .RegWrite(RegWrite), .RegDst(RegDst), .ALUOp(ALUop), .Op(instr_1_op),
    .func(instr_1_func), .ext_op(ext_op), .j_jal(control_1_j_jal), .beq(control_1_beq), .MemToReg(MemToReg),
    .MemWrite(MemWrite), .MemRead(MemRead), .jr(control_1_jr), .NPC(NPC));
  NPCop npcop_1 (.beq(control_1_beq), .j_jal(control_1_j_jal), .jr(control_1_jr), .out_4(NPCop));
  extender extender_1 (.in_1(instr_1_imm16), .out_3(imm32), .in_2(ext_op));
  // Probe on imm32
  Comparator #(.width(32)) comparator_1 (.a(Fwd_RD1_D), .b(Fwd_RD2_D), .eq(comparator_1_eq));  // open: gt, lt
  NPC npc_2 (
    .imm32(imm32), .Jtarget26(Jtarget26), .PC(f_d_reg_1_pc_4_o), .NPC(npc_2_npc), .RegData(Fwd_RD1_D),
    .in_6(NPCop), .equal(comparator_1_eq));
  // Probe on NPCop
  // Probe on f_d_reg_1_instr_o
  D d_1 (.Instr(f_d_reg_1_instr_o), .S1_D(d_1_s1_d), .S2_D(d_1_s2_d), .tuse1_D(d_1_tuse1_d), .tuse2_D(d_1_tuse2_d));
  GRF grf_1 (
    .A1(instr_1_rs), .A2(instr_1_rt), .A3(out_4), .WD(out_5), .RD1(RD1), .RD2(RD2), .clk(Clk), .reset(in_1),
    .we(out_3));
  D_E_reg d_e_reg_1 (
    .pc_i(f_d_reg_1_pc_o), .RD1_i(Fwd_RD1_D), .pc_4_i(f_d_reg_1_pc_4_o), .RD2_i(Fwd_RD2_D),
    .pc_8_i(f_d_reg_1_pc_8_o), .rs_i(instr_1_rs), .rt_i(instr_1_rt), .rd_i(instr_1_rd),
    .instr_i(f_d_reg_1_instr_o), .pc_o(d_e_reg_1_pc_o), .RD1_o(RD1_E), .pc_4_o(d_e_reg_1_pc_4_o),
    .RD2_o(RD2_E), .pc_8_o(d_e_reg_1_pc_8_o), .rt_o(d_e_reg_1_rt_o), .rd_o(d_e_reg_1_rd_o),
    .out_29(d_e_reg_1_out_29), .in_1(Clk), .in_2(in_1), .in_12(flushE), .MemToReg_i(MemToReg),
    .MemToReg_o(d_e_reg_1_memtoreg_o), .MemWrite_i(MemWrite), .MemWrite_o(d_e_reg_1_memwrite_o),
    .MemRead_i(MemRead), .MemRead_o(d_e_reg_1_memread_o), .ALUSrc_i(ALUSrc), .ALUSrc_o(d_e_reg_1_alusrc_o),
    .RegWrite_i(RegWrite), .RegWrite_o(d_e_reg_1_regwrite_o), .RegDst_i(RegDst),
    .RegDst_o(d_e_reg_1_regdst_o), .ALUop_i(ALUop), .ALUop_o(d_e_reg_1_aluop_o), .imm32_2(d_e_reg_1_imm32_2),
    .imm32(imm32));  // open: rs_o
  // Probe on d_e_reg_1_out_29
  Multiplexer #(.select(2), .width(5), .enable("false")) multiplexer_2 (
    .in0(d_e_reg_1_rt_o), .in1(d_e_reg_1_rd_o), .in2({5{1'b1}}), .out(multiplexer_2_out),
    .sel(d_e_reg_1_regdst_o));  // open: in3
  Multiplexer #(.width(32), .enable("false")) multiplexer_3 (
    .in0(Fwd_ALU_B_E), .in1(d_e_reg_1_imm32_2), .out(multiplexer_3_out), .sel(d_e_reg_1_alusrc_o));
  E e_1 (
    .Instr(d_e_reg_1_out_29), .pc_8(d_e_reg_1_pc_8_o), .imm32(d_e_reg_1_imm32_2), .S1_E(e_1_s1_e),
    .S2_E(e_1_s2_e), .DES_E(e_1_des_e), .tnew_E(e_1_tnew_e), .E__D(E__D));
  // Probe on alu_1_out_4
  ALU alu_1 (.in_1(Fwd_ALU_A_E), .in_2(multiplexer_3_out), .out_4(alu_1_out_4), .in_3(d_e_reg_1_aluop_o));
  E_M_reg e_m_reg_1 (
    .aluresult_i(alu_1_out_4), .writedata_i(Fwd_ALU_B_E), .writereg_i(multiplexer_2_out),
    .pc_i(d_e_reg_1_pc_o), .pc_4_i(d_e_reg_1_pc_4_o), .pc_8_i(d_e_reg_1_pc_8_o), .instr_i(d_e_reg_1_out_29),
    .out_18(e_m_reg_1_out_18), .out_19(WD_M), .out_20(e_m_reg_1_out_20), .pc_o(e_m_reg_1_pc_o),
    .pc_4_o(e_m_reg_1_pc_4_o), .pc_8_o(e_m_reg_1_pc_8_o), .out_24(e_m_reg_1_out_24), .in_1(Clk), .in_2(in_1),
    .MemToReg_i(d_e_reg_1_memtoreg_o), .MemToReg_o(e_m_reg_1_memtoreg_o), .MemWrite_i(d_e_reg_1_memwrite_o),
    .MemWrite_o(e_m_reg_1_memwrite_o), .MemRead_i(d_e_reg_1_memread_o), .MemRead_o(e_m_reg_1_memread_o),
    .RegWrite_i(d_e_reg_1_regwrite_o), .RegWrite_o(e_m_reg_1_regwrite_o));
  // Probe on e_m_reg_1_out_18
  // Probe on e_m_reg_1_out_24
  DM dm_1 (
    .in_3(e_m_reg_1_memwrite_o), .in_4(e_m_reg_1_memread_o), .in_5(e_m_reg_1_out_18), .in_6(Fwd_WD_M),
    .out_7(dm_1_out_7), .in_1(Clk), .in_2(in_1));
  // Probe on Fwd_WD_M
  // Probe on dm_1_out_7
  M m_1 (
    .Instr(e_m_reg_1_out_24), .pc_8(e_m_reg_1_pc_8_o), .ALUresult(e_m_reg_1_out_18), .S2_M(m_1_s2_m),
    .DES_M(m_1_des_m), .M__D(M__D), .tnew_M(m_1_tnew_m));
  M_W_reg m_w_reg_1 (
    .writereg_i(e_m_reg_1_out_20), .aluresult_i(e_m_reg_1_out_18), .writedata_i(WD_M),
    .readdata_i(dm_1_out_7), .pc_i(e_m_reg_1_pc_o), .pc_4_i(e_m_reg_1_pc_4_o), .pc_8_i(e_m_reg_1_pc_8_o),
    .instr_i(e_m_reg_1_out_24), .memaddr(e_m_reg_1_out_18), .memdata(Fwd_WD_M),
    .memwrite(e_m_reg_1_memwrite_o), .out_16(out_4), .out_17(ALUresult_W), .out_19(readData_W),
    .pc_8_o(pc_8_W), .out_23(out_2), .out_24({MemAddr_W[31:7], out_7, MemAddr_W[1:0]}), .out_25(out_8),
    .out_26(out_6), .in_1(Clk), .in_2(in_1), .MemToReg(e_m_reg_1_memtoreg_o), .out_27(m_w_reg_1_out_27),
    .RegWrite(e_m_reg_1_regwrite_o), .out_28(out_3));  // open: out_18, pc_o, pc_4_o
  W w_1 (
    .Instr(out_2), .pc_8(pc_8_W), .ALUresult(ALUresult_W), .readData_W(readData_W), .DES_W(w_1_des_w),
    .W__D(W__D), .tnew_W(w_1_tnew_w));
  stallUnit stallunit_1 (
    .s1_D(d_1_s1_d), .s2_D(d_1_s2_d), .tUse1_D(d_1_tuse1_d), .tUse2_D(d_1_tuse2_d), .des_E(e_1_des_e),
    .tNew_E(e_1_tnew_e), .tNew_M(m_1_tnew_m), .des_M(m_1_des_m), .Stall_F(stallF), .Stall_D(stallD),
    .flush_E(flushE));
  Multiplexer #(.select(2), .width(32), .enable("false")) multiplexer_4 (
    .in0(ALUresult_W), .in1(readData_W), .in2(pc_8_W), .out(out_5), .sel(m_w_reg_1_out_27));  // open: in3
  forwardUnit forwardunit_1 (
    .s1_D(d_1_s1_d), .s2_D(d_1_s2_d), .s1_E(e_1_s1_e), .s2_E(e_1_s2_e), .des_E(e_1_des_e),
    .tNew_E(e_1_tnew_e), .s2_M(m_1_s2_m), .tNew_M(m_1_tnew_m), .des_M(m_1_des_m), .tNew_W(w_1_tnew_w),
    .des_W(w_1_des_w), .fRsDsel(forwardunit_1_frsdsel), .fRtDsel(forwardunit_1_frtdsel),
    .fRsEsel(forwardunit_1_frsesel), .fRtEsel(forwardunit_1_frtesel), .fRtMsel(forwardunit_1_frtmsel));
  Multiplexer #(.select(2), .width(32), .enable("false")) multiplexer_5 (
    .in0(RD1), .in1(E__D), .in2(M__D), .in3({32{1'b0}}), .out(Fwd_RD1_D), .sel(forwardunit_1_frsdsel));
  Multiplexer #(.select(2), .width(32), .enable("false")) multiplexer_6 (
    .in0(RD2), .in1(E__D), .in2(M__D), .in3({32{1'b0}}), .out(Fwd_RD2_D), .sel(forwardunit_1_frtdsel));
  Multiplexer #(.select(2), .width(32), .enable("false")) multiplexer_7 (
    .in0(RD1_E), .in1(M__D), .in2(W__D), .in3({32{1'b0}}), .out(Fwd_ALU_A_E), .sel(forwardunit_1_frsesel));
  Multiplexer #(.width(32), .enable("false")) multiplexer_8 (
    .in0(WD_M), .in1(W__D), .out(Fwd_WD_M), .sel(forwardunit_1_frtmsel));
  Multiplexer #(.select(2), .width(32), .enable("false")) multiplexer_9 (
    .in0(RD2_E), .in1(M__D), .in2(W__D), .in3({32{1'b0}}), .out(Fwd_ALU_B_E), .sel(forwardunit_1_frtesel));

  // Other names for the same wires on the sheet: instr_W[31:0] = out_2; MemAddr_W[6:2] = out_7;
  //   MemData_W[31:0] = out_8; MemWrite_W = out_6; RegAddr_W[4:0] = out_4; RegData_W[31:0] = out_5;
  //   RegWrite_W = out_3; reset = in_1

  // Notes on the sheet:
  //   contents of rom_1 (hex, n*v repeats v):
  //   34021234 ac020000 8c010000 10220003 0 c000c08 0 34050005 34060006
endmodule

module stallUnit (
  input  [4:0] s1_D,
  input  [4:0] s2_D,
  input  [1:0] tUse1_D,
  input  [1:0] tUse2_D,
  input  [4:0] des_E,
  input  [3:0] tNew_E,
  input  [3:0] tNew_M,
  input  [4:0] des_M,
  output Stall_F,
  output Stall_D,
  output flush_E
);

  wire and_1_out, and_2_out, and_3_out, and_4_out, comparator_1_eq, comparator_2_eq, comparator_3_lt,
       comparator_4_eq, comparator_5_eq, comparator_6_lt, comparator_7_eq, comparator_8_eq, comparator_9_lt,
       comparator_10_eq, comparator_11_eq, comparator_12_lt, not_1_out, not_2_out, not_3_out, not_4_out;
  wire [3:0] tUse1_D_t, tUse2_D_t;

  Comparator #(.width(5), .mode("unsigned")) comparator_1 (
    .a(s1_D), .b({5{1'b0}}), .eq(comparator_1_eq));  // open: gt, lt
  Comparator #(.width(5), .mode("unsigned")) comparator_2 (.a(s1_D), .b(des_E), .eq(comparator_2_eq));  // open: gt, lt
  Comparator #(.width(4), .mode("unsigned")) comparator_3 (
    .a(tUse1_D_t), .b(tNew_E), .lt(comparator_3_lt));  // open: gt, eq
  Comparator #(.width(5), .mode("unsigned")) comparator_4 (
    .a(s2_D), .b({5{1'b0}}), .eq(comparator_4_eq));  // open: gt, lt
  Comparator #(.width(5), .mode("unsigned")) comparator_5 (.a(s2_D), .b(des_E), .eq(comparator_5_eq));  // open: gt, lt
  Comparator #(.width(4), .mode("unsigned")) comparator_6 (
    .a(tUse2_D_t), .b(tNew_E), .lt(comparator_6_lt));  // open: gt, eq
  Comparator #(.width(5), .mode("unsigned")) comparator_7 (
    .a(s1_D), .b({5{1'b0}}), .eq(comparator_7_eq));  // open: gt, lt
  Comparator #(.width(5), .mode("unsigned")) comparator_8 (.a(s1_D), .b(des_M), .eq(comparator_8_eq));  // open: gt, lt
  Comparator #(.width(4), .mode("unsigned")) comparator_9 (
    .a(tUse1_D_t), .b(tNew_M), .lt(comparator_9_lt));  // open: gt, eq
  Comparator #(.width(5), .mode("unsigned")) comparator_10 (
    .a(s2_D), .b({5{1'b0}}), .eq(comparator_10_eq));  // open: gt, lt
  Comparator #(.width(5), .mode("unsigned")) comparator_11 (
    .a(s2_D), .b(des_M), .eq(comparator_11_eq));  // open: gt, lt
  Comparator #(.width(4), .mode("unsigned")) comparator_12 (
    .a(tUse2_D_t), .b(tNew_M), .lt(comparator_12_lt));  // open: gt, eq
  assign tUse1_D_t = {{2{1'b0}}, tUse1_D};  // Bit_Extender bit_extender_1
  not not_1 (not_1_out, comparator_1_eq);
  not not_2 (not_2_out, comparator_4_eq);
  not not_3 (not_3_out, comparator_7_eq);
  not not_4 (not_4_out, comparator_10_eq);
  and and_1 (and_1_out, not_1_out, comparator_2_eq, comparator_3_lt);
  and and_2 (and_2_out, not_2_out, comparator_5_eq, comparator_6_lt);
  and and_3 (and_3_out, not_3_out, comparator_8_eq, comparator_9_lt);
  and and_4 (and_4_out, not_4_out, comparator_11_eq, comparator_12_lt);
  assign tUse2_D_t = {{2{1'b0}}, tUse2_D};  // Bit_Extender bit_extender_2
  or or_1 (flush_E, and_1_out, and_2_out, and_3_out, and_4_out);

  assign Stall_D = flush_E;
  assign Stall_F = flush_E;

  // Other names for the same wires on the sheet: stall_flag = flush_E
endmodule

module forwardUnit (
  input  [4:0] s1_D,
  input  [4:0] s2_D,
  input  [4:0] s1_E,
  input  [4:0] s2_E,
  input  [4:0] des_E,
  input  [3:0] tNew_E,
  input  [4:0] s2_M,
  input  [3:0] tNew_M,
  input  [4:0] des_M,
  input  [3:0] tNew_W,
  input  [4:0] des_W,
  output [1:0] fRsDsel,
  output [1:0] fRtDsel,
  output [1:0] fRsEsel,
  output [1:0] fRtEsel,
  output fRtMsel
);

  wire and_1_out, and_2_out, and_3_out, and_4_out, and_5_out, and_6_out, and_7_out, and_8_out, and_9_out,
       comparator_1_eq, comparator_2_eq, comparator_3_eq, comparator_4_eq, comparator_5_eq, comparator_6_eq,
       comparator_7_eq, comparator_8_eq, comparator_9_eq, comparator_10_eq, comparator_11_eq,
       comparator_12_eq, comparator_13_eq, comparator_14_eq, comparator_15_eq, comparator_16_eq,
       comparator_17_eq, comparator_18_eq, comparator_19_eq, comparator_20_eq, comparator_21_eq,
       comparator_22_eq, comparator_23_eq, comparator_24_eq, comparator_25_eq, comparator_26_eq,
       comparator_27_eq, not_1_out, not_2_out, not_3_out, not_4_out, not_5_out, not_6_out, not_7_out,
       not_8_out, not_9_out;
  wire [1:0] multiplexer_1_out, multiplexer_2_out, multiplexer_5_out, multiplexer_6_out;

  not not_1 (not_1_out, comparator_1_eq);
  Comparator #(.width(5), .mode("unsigned")) comparator_1 (
    .a(s1_D), .b({5{1'b0}}), .eq(comparator_1_eq));  // open: gt, lt
  Comparator #(.width(5), .mode("unsigned")) comparator_2 (.a(s1_D), .b(des_M), .eq(comparator_2_eq));  // open: gt, lt
  Comparator #(.width(4), .mode("unsigned")) comparator_3 (
    .a(tNew_M), .b(4'b0000), .eq(comparator_3_eq));  // open: gt, lt
  not not_2 (not_2_out, comparator_4_eq);
  Comparator #(.width(5), .mode("unsigned")) comparator_4 (
    .a(s1_D), .b({5{1'b0}}), .eq(comparator_4_eq));  // open: gt, lt
  Comparator #(.width(5), .mode("unsigned")) comparator_5 (.a(s1_D), .b(des_E), .eq(comparator_5_eq));  // open: gt, lt
  Comparator #(.width(4), .mode("unsigned")) comparator_6 (
    .a(tNew_E), .b(4'b0000), .eq(comparator_6_eq));  // open: gt, lt
  Comparator #(.width(5), .mode("unsigned")) comparator_7 (
    .a(s2_D), .b({5{1'b0}}), .eq(comparator_7_eq));  // open: gt, lt
  Comparator #(.width(5), .mode("unsigned")) comparator_8 (.a(s2_D), .b(des_M), .eq(comparator_8_eq));  // open: gt, lt
  Comparator #(.width(4), .mode("unsigned")) comparator_9 (
    .a(tNew_M), .b(4'b0000), .eq(comparator_9_eq));  // open: gt, lt
  Comparator #(.width(5), .mode("unsigned")) comparator_10 (
    .a(s2_D), .b({5{1'b0}}), .eq(comparator_10_eq));  // open: gt, lt
  Comparator #(.width(5), .mode("unsigned")) comparator_11 (
    .a(s2_D), .b(des_E), .eq(comparator_11_eq));  // open: gt, lt
  Comparator #(.width(4), .mode("unsigned")) comparator_12 (
    .a(tNew_E), .b(4'b0000), .eq(comparator_12_eq));  // open: gt, lt
  and and_1 (and_1_out, not_1_out, comparator_2_eq, comparator_3_eq);
  and and_2 (and_2_out, not_2_out, comparator_5_eq, comparator_6_eq);
  not not_3 (not_3_out, comparator_7_eq);
  not not_4 (not_4_out, comparator_10_eq);
  Multiplexer #(.width(2)) multiplexer_1 (
    .in0(2'b00), .in1(2'b10), .out(multiplexer_1_out), .sel(and_1_out));  // open: en
  and and_3 (and_3_out, not_3_out, comparator_8_eq, comparator_9_eq);
  and and_4 (and_4_out, not_4_out, comparator_11_eq, comparator_12_eq);
  Multiplexer #(.width(2)) multiplexer_2 (
    .in0(2'b00), .in1(2'b10), .out(multiplexer_2_out), .sel(and_3_out));  // open: en
  Multiplexer #(.width(2)) multiplexer_3 (
    .in0(multiplexer_1_out), .in1(2'b01), .out(fRsDsel), .sel(and_2_out));  // open: en
  Multiplexer #(.width(2)) multiplexer_4 (
    .in0(multiplexer_2_out), .in1(2'b01), .out(fRtDsel), .sel(and_4_out));  // open: en
  Comparator #(.width(5), .mode("unsigned")) comparator_13 (
    .a(s1_E), .b({5{1'b0}}), .eq(comparator_13_eq));  // open: gt, lt
  Comparator #(.width(5), .mode("unsigned")) comparator_14 (
    .a(s1_E), .b(des_W), .eq(comparator_14_eq));  // open: gt, lt
  Comparator #(.width(4), .mode("unsigned")) comparator_15 (
    .a(tNew_W), .b(4'b0000), .eq(comparator_15_eq));  // open: gt, lt
  Comparator #(.width(5), .mode("unsigned")) comparator_16 (
    .a(s1_E), .b({5{1'b0}}), .eq(comparator_16_eq));  // open: gt, lt
  Comparator #(.width(5), .mode("unsigned")) comparator_17 (
    .a(s1_E), .b(des_M), .eq(comparator_17_eq));  // open: gt, lt
  Comparator #(.width(4), .mode("unsigned")) comparator_18 (
    .a(tNew_M), .b(4'b0000), .eq(comparator_18_eq));  // open: gt, lt
  Comparator #(.width(5), .mode("unsigned")) comparator_19 (
    .a(s2_E), .b({5{1'b0}}), .eq(comparator_19_eq));  // open: gt, lt
  Comparator #(.width(5), .mode("unsigned")) comparator_20 (
    .a(s2_E), .b(des_W), .eq(comparator_20_eq));  // open: gt, lt
  Comparator #(.width(4), .mode("unsigned")) comparator_21 (
    .a(tNew_W), .b(4'b0000), .eq(comparator_21_eq));  // open: gt, lt
  Comparator #(.width(5), .mode("unsigned")) comparator_22 (
    .a(s2_E), .b({5{1'b0}}), .eq(comparator_22_eq));  // open: gt, lt
  Comparator #(.width(5), .mode("unsigned")) comparator_23 (
    .a(s2_E), .b(des_M), .eq(comparator_23_eq));  // open: gt, lt
  Comparator #(.width(4), .mode("unsigned")) comparator_24 (
    .a(tNew_M), .b(4'b0000), .eq(comparator_24_eq));  // open: gt, lt
  not not_5 (not_5_out, comparator_13_eq);
  not not_6 (not_6_out, comparator_16_eq);
  not not_7 (not_7_out, comparator_19_eq);
  not not_8 (not_8_out, comparator_22_eq);
  and and_5 (and_5_out, not_5_out, comparator_14_eq, comparator_15_eq);
  and and_6 (and_6_out, not_6_out, comparator_17_eq, comparator_18_eq);
  and and_7 (and_7_out, not_7_out, comparator_20_eq, comparator_21_eq);
  and and_8 (and_8_out, not_8_out, comparator_23_eq, comparator_24_eq);
  Multiplexer #(.width(2)) multiplexer_5 (
    .in0(2'b00), .in1(2'b10), .out(multiplexer_5_out), .sel(and_5_out));  // open: en
  Multiplexer #(.width(2)) multiplexer_6 (
    .in0(2'b00), .in1(2'b10), .out(multiplexer_6_out), .sel(and_7_out));  // open: en
  Multiplexer #(.width(2)) multiplexer_7 (
    .in0(multiplexer_5_out), .in1(2'b01), .out(fRsEsel), .sel(and_6_out));  // open: en
  Multiplexer #(.width(2)) multiplexer_8 (
    .in0(multiplexer_6_out), .in1(2'b01), .out(fRtEsel), .sel(and_8_out));  // open: en
  Comparator #(.width(5), .mode("unsigned")) comparator_25 (
    .a(s2_M), .b({5{1'b0}}), .eq(comparator_25_eq));  // open: gt, lt
  not not_9 (not_9_out, comparator_25_eq);
  Comparator #(.width(5), .mode("unsigned")) comparator_26 (
    .a(s2_M), .b(des_W), .eq(comparator_26_eq));  // open: gt, lt
  Comparator #(.width(4), .mode("unsigned")) comparator_27 (
    .a(tNew_W), .b(4'b0000), .eq(comparator_27_eq));  // open: gt, lt
  and and_9 (and_9_out, not_9_out, comparator_26_eq, comparator_27_eq);
  Multiplexer multiplexer_9 (.in0(1'b0), .in1(1'b1), .out(fRtMsel), .sel(and_9_out));  // open: en
endmodule

module F_D_reg (
  input  in_1,
  input  in_2,
  input  [31:0] instr_i,
  input  [31:0] pc_i,
  input  [31:0] pc_4_i,
  input  [31:0] pc_8_i,
  input  in_7,
  output [31:0] instr_o,
  output [31:0] pc_o,
  output [31:0] pc_4_o,
  output [31:0] pc_8_o
);

  wire clk_prime, not_1_out, not_2_out, not_3_out, not_4_out;

  not not_1 (not_1_out, in_7);
  not not_2 (not_2_out, in_7);
  buf and_1 (clk_prime, in_1);  // AND_Gate
  Register #(.width(32)) register_1 (.D(instr_i), .en(not_1_out), .Q(instr_o), .clk(clk_prime), .clr(in_2));
  Register #(.width(32)) register_2 (.D(pc_i), .en(not_2_out), .Q(pc_o), .clk(clk_prime), .clr(in_2));
  Register #(.width(32)) register_3 (.D(pc_4_i), .en(not_3_out), .Q(pc_4_o), .clk(clk_prime), .clr(in_2));
  not not_3 (not_3_out, in_7);
  Register #(.width(32)) register_4 (.D(pc_8_i), .en(not_4_out), .Q(pc_8_o), .clk(clk_prime), .clr(in_2));
  not not_4 (not_4_out, in_7);

  // Other names for the same wires on the sheet: clk = in_1; F_D_stall = in_7; reset = in_2
endmodule

module D_E_reg (
  input  in_1,
  input  in_2,
  input  [31:0] pc_i,
  input  [31:0] RD1_i,
  input  [31:0] pc_4_i,
  input  [31:0] RD2_i,
  input  [31:0] pc_8_i,
  input  [4:0] rs_i,
  input  [4:0] rt_i,
  input  [4:0] rd_i,
  input  [31:0] instr_i,
  input  in_12,
  input  [1:0] MemToReg_i,
  input  MemWrite_i,
  input  MemRead_i,
  input  ALUSrc_i,
  input  RegWrite_i,
  input  [1:0] RegDst_i,
  input  [3:0] ALUop_i,
  input  [31:0] imm32,
  output [31:0] pc_o,
  output [31:0] RD1_o,
  output [31:0] pc_4_o,
  output [31:0] RD2_o,
  output [31:0] pc_8_o,
  output [4:0] rs_o,
  output [4:0] rt_o,
  output [4:0] rd_o,
  output [31:0] out_29,
  output [1:0] MemToReg_o,
  output MemWrite_o,
  output MemRead_o,
  output ALUSrc_o,
  output RegWrite_o,
  output [1:0] RegDst_o,
  output [3:0] ALUop_o,
  output [31:0] imm32_2
);

  wire multiplexer_8_out, multiplexer_9_out, multiplexer_10_out, multiplexer_11_out;
  wire [1:0] multiplexer_7_out, multiplexer_12_out;
  wire [3:0] multiplexer_13_out;
  wire [4:0] multiplexer_3_out, multiplexer_4_out, multiplexer_5_out;
  wire [31:0] multiplexer_1_out, multiplexer_2_out, multiplexer_6_out, multiplexer_14_out,
       multiplexer_15_out, multiplexer_16_out, multiplexer_17_out;

  Multiplexer #(.width(32), .enable("false")) multiplexer_1 (
    .in0(RD1_i), .in1({32{1'b0}}), .out(multiplexer_1_out), .sel(in_12));
  Multiplexer #(.width(32), .enable("false")) multiplexer_2 (
    .in0(RD2_i), .in1({32{1'b0}}), .out(multiplexer_2_out), .sel(in_12));
  Multiplexer #(.width(5), .enable("false")) multiplexer_3 (
    .in0(rs_i), .in1({5{1'b0}}), .out(multiplexer_3_out), .sel(in_12));
  Multiplexer #(.width(5), .enable("false")) multiplexer_4 (
    .in0(rt_i), .in1({5{1'b0}}), .out(multiplexer_4_out), .sel(in_12));
  Multiplexer #(.width(5), .enable("false")) multiplexer_5 (
    .in0(rd_i), .in1({5{1'b0}}), .out(multiplexer_5_out), .sel(in_12));
  Multiplexer #(.width(32), .enable("false")) multiplexer_6 (
    .in0(instr_i), .in1({32{1'b0}}), .out(multiplexer_6_out), .sel(in_12));
  Multiplexer #(.width(2), .enable("false")) multiplexer_7 (
    .in0(MemToReg_i), .in1(2'b00), .out(multiplexer_7_out), .sel(in_12));
  Multiplexer #(.enable("false")) multiplexer_8 (.in0(MemWrite_i), .in1(1'b0), .out(multiplexer_8_out), .sel(in_12));
  Multiplexer #(.enable("false")) multiplexer_9 (.in0(MemRead_i), .in1(1'b0), .out(multiplexer_9_out), .sel(in_12));
  Multiplexer #(.enable("false")) multiplexer_10 (.in0(ALUSrc_i), .in1(1'b0), .out(multiplexer_10_out), .sel(in_12));
  Multiplexer #(.enable("false")) multiplexer_11 (.in0(RegWrite_i), .in1(1'b0), .out(multiplexer_11_out), .sel(in_12));
  Multiplexer #(.width(2), .enable("false")) multiplexer_12 (
    .in0(RegDst_i), .in1(2'b00), .out(multiplexer_12_out), .sel(in_12));
  Multiplexer #(.width(4), .enable("false")) multiplexer_13 (
    .in0(ALUop_i), .in1(4'b0000), .out(multiplexer_13_out), .sel(in_12));
  Multiplexer #(.width(32), .enable("false")) multiplexer_14 (
    .in0(imm32), .in1({32{1'b0}}), .out(multiplexer_14_out), .sel(in_12));
  Register #(.width(32)) register_1 (.D(multiplexer_1_out), .Q(RD1_o), .clk(in_1), .clr(in_2));  // open: en
  Register #(.width(32)) register_2 (.D(multiplexer_2_out), .Q(RD2_o), .clk(in_1), .clr(in_2));  // open: en
  Register #(.width(5)) register_3 (.D(multiplexer_3_out), .Q(rs_o), .clk(in_1), .clr(in_2));  // open: en
  Register #(.width(5)) register_4 (.D(multiplexer_4_out), .Q(rt_o), .clk(in_1), .clr(in_2));  // open: en
  Register #(.width(5)) register_5 (.D(multiplexer_5_out), .Q(rd_o), .clk(in_1), .clr(in_2));  // open: en
  Register #(.width(32)) register_6 (.D(multiplexer_6_out), .Q(out_29), .clk(in_1), .clr(in_2));  // open: en
  Register #(.width(1)) register_7 (.D(multiplexer_11_out), .Q(RegWrite_o), .clk(in_1), .clr(in_2));  // open: en
  Register #(.width(2)) register_8 (.D(multiplexer_12_out), .Q(RegDst_o), .clk(in_1), .clr(in_2));  // open: en
  Register #(.width(4)) register_9 (.D(multiplexer_13_out), .Q(ALUop_o), .clk(in_1), .clr(in_2));  // open: en
  Register #(.width(32)) register_10 (.D(multiplexer_14_out), .Q(imm32_2), .clk(in_1), .clr(in_2));  // open: en
  Register #(.width(2)) register_11 (.D(multiplexer_7_out), .Q(MemToReg_o), .clk(in_1), .clr(in_2));  // open: en
  Register #(.width(1)) register_12 (.D(multiplexer_8_out), .Q(MemWrite_o), .clk(in_1), .clr(in_2));  // open: en
  Register #(.width(1)) register_13 (.D(multiplexer_9_out), .Q(MemRead_o), .clk(in_1), .clr(in_2));  // open: en
  Register #(.width(1)) register_14 (.D(multiplexer_10_out), .Q(ALUSrc_o), .clk(in_1), .clr(in_2));  // open: en
  Multiplexer #(.width(32), .enable("false")) multiplexer_15 (
    .in0(pc_i), .in1({32{1'b0}}), .out(multiplexer_15_out), .sel(in_12));
  Multiplexer #(.width(32), .enable("false")) multiplexer_16 (
    .in0(pc_4_i), .in1({32{1'b0}}), .out(multiplexer_16_out), .sel(in_12));
  Multiplexer #(.width(32), .enable("false")) multiplexer_17 (
    .in0(pc_8_i), .in1({32{1'b0}}), .out(multiplexer_17_out), .sel(in_12));
  Register #(.width(32)) register_15 (.D(multiplexer_15_out), .Q(pc_o), .clk(in_1), .clr(in_2));  // open: en
  Register #(.width(32)) register_16 (.D(multiplexer_16_out), .Q(pc_4_o), .clk(in_1), .clr(in_2));  // open: en
  Register #(.width(32)) register_17 (.D(multiplexer_17_out), .Q(pc_8_o), .clk(in_1), .clr(in_2));  // open: en

  // Other names for the same wires on the sheet: clk = in_1; clk_prime = in_1; flush = in_12; Reset = in_2
endmodule

module E_M_reg (
  input  in_1,
  input  in_2,
  input  [1:0] MemToReg_i,
  input  MemWrite_i,
  input  MemRead_i,
  input  RegWrite_i,
  input  [31:0] aluresult_i,
  input  [31:0] writedata_i,
  input  [4:0] writereg_i,
  input  [31:0] pc_i,
  input  [31:0] pc_4_i,
  input  [31:0] pc_8_i,
  input  [31:0] instr_i,
  output [1:0] MemToReg_o,
  output MemWrite_o,
  output MemRead_o,
  output RegWrite_o,
  output [31:0] out_18,
  output [31:0] out_19,
  output [4:0] out_20,
  output [31:0] pc_o,
  output [31:0] pc_4_o,
  output [31:0] pc_8_o,
  output [31:0] out_24
);

  Register #(.width(1)) register_1 (.D(MemRead_i), .Q(MemRead_o), .clk(in_1), .clr(in_2));  // open: en
  Register #(.width(32)) register_2 (.D(aluresult_i), .Q(out_18), .clk(in_1), .clr(in_2));  // open: en
  Register #(.width(32)) register_3 (.D(writedata_i), .Q(out_19), .clk(in_1), .clr(in_2));  // open: en
  Register #(.width(5)) register_4 (.D(writereg_i), .Q(out_20), .clk(in_1), .clr(in_2));  // open: en
  Register #(.width(32)) register_5 (.D(pc_i), .Q(pc_o), .clk(in_1), .clr(in_2));  // open: en
  Register #(.width(32)) register_6 (.D(pc_4_i), .Q(pc_4_o), .clk(in_1), .clr(in_2));  // open: en
  Register #(.width(32)) register_7 (.D(pc_8_i), .Q(pc_8_o), .clk(in_1), .clr(in_2));  // open: en
  Register #(.width(32)) register_8 (.D(instr_i), .Q(out_24), .clk(in_1), .clr(in_2));  // open: en
  Register #(.width(2)) register_9 (.D(MemToReg_i), .Q(MemToReg_o), .clk(in_1), .clr(in_2));  // open: en
  Register #(.width(1)) register_10 (.D(MemWrite_i), .Q(MemWrite_o), .clk(in_1), .clr(in_2));  // open: en
  Register #(.width(1)) register_11 (.D(RegWrite_i), .Q(RegWrite_o), .clk(in_1), .clr(in_2));  // open: en

  // Other names for the same wires on the sheet: clk = in_1; clk_prime = in_1; Reset = in_2
endmodule

module M_W_reg (
  input  in_1,
  input  in_2,
  input  [4:0] writereg_i,
  input  [31:0] aluresult_i,
  input  [31:0] writedata_i,
  input  [31:0] readdata_i,
  input  [31:0] pc_i,
  input  [31:0] pc_4_i,
  input  [31:0] pc_8_i,
  input  [31:0] instr_i,
  input  [31:0] memaddr,
  input  [31:0] memdata,
  input  memwrite,
  input  [1:0] MemToReg,
  input  RegWrite,
  output [4:0] out_16,
  output [31:0] out_17,
  output [31:0] out_18,
  output [31:0] out_19,
  output [31:0] pc_o,
  output [31:0] pc_4_o,
  output [31:0] pc_8_o,
  output [31:0] out_23,
  output [31:0] out_24,
  output [31:0] out_25,
  output out_26,
  output [1:0] out_27,
  output out_28
);

  Register #(.width(5)) register_1 (.D(writereg_i), .Q(out_16), .clk(in_1), .clr(in_2));  // open: en
  Register #(.width(32)) register_2 (.D(aluresult_i), .Q(out_17), .clk(in_1), .clr(in_2));  // open: en
  Register #(.width(32)) register_3 (.D(writedata_i), .Q(out_18), .clk(in_1), .clr(in_2));  // open: en
  Register #(.width(32)) register_4 (.D(readdata_i), .Q(out_19), .clk(in_1), .clr(in_2));  // open: en
  Register #(.width(32)) register_5 (.D(pc_i), .Q(pc_o), .clk(in_1), .clr(in_2));  // open: en
  Register #(.width(32)) register_6 (.D(pc_4_i), .Q(pc_4_o), .clk(in_1), .clr(in_2));  // open: en
  Register #(.width(32)) register_7 (.D(pc_8_i), .Q(pc_8_o), .clk(in_1), .clr(in_2));  // open: en
  Register #(.width(32)) register_8 (.D(instr_i), .Q(out_23), .clk(in_1), .clr(in_2));  // open: en
  Register #(.width(32)) register_9 (.D(memaddr), .Q(out_24), .clk(in_1), .clr(in_2));  // open: en
  Register #(.width(32)) register_10 (.D(memdata), .Q(out_25), .clk(in_1), .clr(in_2));  // open: en
  Register #(.width(1)) register_11 (.D(memwrite), .Q(out_26), .clk(in_1), .clr(in_2));  // open: en
  Register #(.width(2)) register_12 (.D(MemToReg), .Q(out_27), .clk(in_1), .clr(in_2));  // open: en
  Register #(.width(1)) register_13 (.D(RegWrite), .Q(out_28), .clk(in_1), .clr(in_2));  // open: en

  // Other names for the same wires on the sheet: clk = in_1; clk_prime = in_1; Reset = in_2
endmodule

module GRF (
  input  [4:0] A1,
  input  clk,
  input  reset,
  input  we,
  input  [4:0] A2,
  input  [4:0] A3,
  input  [31:0] WD,
  output [31:0] RD1,
  output [31:0] RD2
);

  wire CLK_t;
  wire [31:0] I0, I1, I2, I3, I4, I5, I6, I7, I8, I9, I10, I11, I12, I13, I14, I15, I16, I17, I18, I19, I20,
       I21, I22, I23, I24, I25, I26, I27, I28, I29, I30, I31, O0, O1, O2, O3, O4, O5, O6, O7, O8, O9, O10,
       O11, O12, O13, O14, O15, O16, O17, O18, O19, O20, O21, O22, O23, O24, O25, O26, O27, O28, O29, O30,
       O31;

  Demultiplexer #(.select(5), .width(32), .tristate("true")) demultiplexer_1 (
    .out0(I0), .out1(I1), .out2(I2), .out3(I3), .out4(I4), .out5(I5), .out6(I6), .out7(I7), .out8(I8),
    .out9(I9), .out10(I10), .out11(I11), .out12(I12), .out13(I13), .out14(I14), .out15(I15), .out16(I16),
    .out17(I17), .out18(I18), .out19(I19), .out20(I20), .out21(I21), .out22(I22), .out23(I23), .out24(I24),
    .out25(I25), .out26(I26), .out27(I27), .out28(I28), .out29(I29), .out30(I30), .out31(I31), .in(WD),
    .sel(A3));  // open: en
  not not_1 (CLK_t, clk);
  Multiplexer #(.select(5), .width(32)) multiplexer_1 (
    .in0(O0), .in1(O1), .in2(O2), .in3(O3), .in4(O4), .in5(O5), .in6(O6), .in7(O7), .in8(O8), .in9(O9),
    .in10(O10), .in11(O11), .in12(O12), .in13(O13), .in14(O14), .in15(O15), .in16(O16), .in17(O17),
    .in18(O18), .in19(O19), .in20(O20), .in21(O21), .in22(O22), .in23(O23), .in24(O24), .in25(O25),
    .in26(O26), .in27(O27), .in28(O28), .in29(O29), .in30(O30), .in31(O31), .out(RD2), .sel(A2));  // open: en
  Multiplexer #(.select(5), .width(32)) multiplexer_2 (
    .in0(O0), .in1(O1), .in2(O2), .in3(O3), .in4(O4), .in5(O5), .in6(O6), .in7(O7), .in8(O8), .in9(O9),
    .in10(O10), .in11(O11), .in12(O12), .in13(O13), .in14(O14), .in15(O15), .in16(O16), .in17(O17),
    .in18(O18), .in19(O19), .in20(O20), .in21(O21), .in22(O22), .in23(O23), .in24(O24), .in25(O25),
    .in26(O26), .in27(O27), .in28(O28), .in29(O29), .in30(O30), .in31(O31), .out(RD1), .sel(A1));  // open: en
  Register #(.width(32)) register_1 (.D({32{1'b0}}), .en(we), .Q(O0), .clk(CLK_t), .clr(reset));
  Register #(.width(32)) register_2 (.D(I8), .en(we), .Q(O8), .clk(CLK_t), .clr(reset));
  Register #(.width(32)) register_3 (.D(I16), .en(we), .Q(O16), .clk(CLK_t), .clr(reset));
  Register #(.width(32)) register_4 (.D(I24), .en(we), .Q(O24), .clk(CLK_t), .clr(reset));
  Register #(.width(32)) register_5 (.D(I1), .en(we), .Q(O1), .clk(CLK_t), .clr(reset));
  Register #(.width(32)) register_6 (.D(I9), .en(we), .Q(O9), .clk(CLK_t), .clr(reset));
  Register #(.width(32)) register_7 (.D(I17), .en(we), .Q(O17), .clk(CLK_t), .clr(reset));
  Register #(.width(32)) register_8 (.D(I25), .en(we), .Q(O25), .clk(CLK_t), .clr(reset));
  Register #(.width(32)) register_9 (.D(I2), .en(we), .Q(O2), .clk(CLK_t), .clr(reset));
  Register #(.width(32)) register_10 (.D(I10), .en(we), .Q(O10), .clk(CLK_t), .clr(reset));
  Register #(.width(32)) register_11 (.D(I18), .en(we), .Q(O18), .clk(CLK_t), .clr(reset));
  Register #(.width(32)) register_12 (.D(I26), .en(we), .Q(O26), .clk(CLK_t), .clr(reset));
  Register #(.width(32)) register_13 (.D(I3), .en(we), .Q(O3), .clk(CLK_t), .clr(reset));
  Register #(.width(32)) register_14 (.D(I11), .en(we), .Q(O11), .clk(CLK_t), .clr(reset));
  Register #(.width(32)) register_15 (.D(I19), .en(we), .Q(O19), .clk(CLK_t), .clr(reset));
  Register #(.width(32)) register_16 (.D(I27), .en(we), .Q(O27), .clk(CLK_t), .clr(reset));
  Register #(.width(32)) register_17 (.D(I4), .en(we), .Q(O4), .clk(CLK_t), .clr(reset));
  Register #(.width(32)) register_18 (.D(I12), .en(we), .Q(O12), .clk(CLK_t), .clr(reset));
  Register #(.width(32)) register_19 (.D(I20), .en(we), .Q(O20), .clk(CLK_t), .clr(reset));
  Register #(.width(32)) register_20 (.D(I28), .en(we), .Q(O28), .clk(CLK_t), .clr(reset));
  Register #(.width(32)) register_21 (.D(I5), .en(we), .Q(O5), .clk(CLK_t), .clr(reset));
  Register #(.width(32)) register_22 (.D(I13), .en(we), .Q(O13), .clk(CLK_t), .clr(reset));
  Register #(.width(32)) register_23 (.D(I21), .en(we), .Q(O21), .clk(CLK_t), .clr(reset));
  Register #(.width(32)) register_24 (.D(I29), .en(we), .Q(O29), .clk(CLK_t), .clr(reset));
  Register #(.width(32)) register_25 (.D(I6), .en(we), .Q(O6), .clk(CLK_t), .clr(reset));
  Register #(.width(32)) register_26 (.D(I14), .en(we), .Q(O14), .clk(CLK_t), .clr(reset));
  Register #(.width(32)) register_27 (.D(I22), .en(we), .Q(O22), .clk(CLK_t), .clr(reset));
  Register #(.width(32)) register_28 (.D(I30), .en(we), .Q(O30), .clk(CLK_t), .clr(reset));
  Register #(.width(32)) register_29 (.D(I7), .en(we), .Q(O7), .clk(CLK_t), .clr(reset));
  Register #(.width(32)) register_30 (.D(I15), .en(we), .Q(O15), .clk(CLK_t), .clr(reset));
  Register #(.width(32)) register_31 (.D(I23), .en(we), .Q(O23), .clk(CLK_t), .clr(reset));
  Register #(.width(32)) register_32 (.D(I31), .en(we), .Q(O31), .clk(CLK_t), .clr(reset));
endmodule

module ALU (
  input  [31:0] in_1,
  input  [31:0] in_2,
  input  [3:0] in_3,
  output [31:0] out_4
);

  wire comparator_1_lt, comparator_2_lt;
  wire [31:0] adder_1_out, and_1_out, bit_extender_1_out, bit_extender_2_out, nor_1_out, or_1_out,
       shifter_1_out, shifter_2_out, shifter_3_out, subtractor_1_out, xor_1_out;

  Shifter #(.width(32)) shifter_1 (.in(in_1), .\dist (in_2[4:0]), .out(shifter_1_out));
  Shifter #(.width(32), .shift("ar")) shifter_2 (.in(in_1), .\dist (in_2[4:0]), .out(shifter_2_out));
  Shifter #(.width(32), .shift("lr")) shifter_3 (.in(in_1), .\dist (in_2[4:0]), .out(shifter_3_out));
  Adder #(.width(32)) adder_1 (.a(in_1), .b(in_2), .out(adder_1_out));  // open: cin, cout
  Subtractor #(.width(32)) subtractor_1 (.a(in_1), .b(in_2), .out(subtractor_1_out));  // open: bin, bout
  assign and_1_out = in_1 & in_2;  // AND_Gate and_1, 32 bits wide
  assign or_1_out = in_1 | in_2;  // OR_Gate or_1, 32 bits wide
  assign xor_1_out = in_1 ^ in_2;  // XOR_Gate xor_1, 32 bits wide
  assign nor_1_out = ~(in_1 | in_2);  // NOR_Gate nor_1, 32 bits wide
  Comparator #(.width(32)) comparator_1 (.a(in_1), .b(in_2), .lt(comparator_1_lt));  // open: gt, eq
  Comparator #(.width(32), .mode("unsigned")) comparator_2 (.a(in_1), .b(in_2), .lt(comparator_2_lt));  // open: gt, eq
  assign bit_extender_1_out = {{31{1'b0}}, comparator_1_lt};  // Bit_Extender bit_extender_1
  assign bit_extender_2_out = {{31{1'b0}}, comparator_2_lt};  // Bit_Extender bit_extender_2
  Multiplexer #(.select(4), .width(32)) multiplexer_1 (
    .in0(shifter_1_out), .in1(shifter_2_out), .in2(shifter_3_out), .in4(in_2), .in5(adder_1_out),
    .in6(subtractor_1_out), .in7(and_1_out), .in8(or_1_out), .in9(xor_1_out), .in10(nor_1_out),
    .in11(bit_extender_1_out), .in12(bit_extender_2_out), .out(out_4), .sel(in_3));  // open: in3, in13, in14, in15, en
endmodule

module control (
  input  [5:0] Op,
  input  [5:0] func,
  output [1:0] RegDst,
  output MemWrite,
  output beq,
  output j_jal,
  output jr,
  output [1:0] ext_op,
  output RegWrite,
  output ALUSrc,
  output MemRead,
  output [1:0] MemToReg,
  output NPC,
  output [3:0] ALUOp
);

  wire addu, j, nop, not_1_out, not_2_out, not_3_out, not_4_out, not_5_out, not_6_out, not_7_out, not_8_out,
       not_9_out, not_10_out, not_11_out, not_12_out, ori, R, subu;

  not not_1 (not_1_out, Op[5]);
  not not_2 (not_2_out, Op[4]);
  not not_3 (not_3_out, Op[3]);
  not not_4 (not_4_out, Op[2]);
  not not_5 (not_5_out, Op[1]);
  not not_6 (not_6_out, Op[0]);
  and u_R (R, not_1_out, not_2_out, not_3_out, not_4_out, not_5_out, not_6_out);
  and lw (MemRead, Op[5], not_2_out, not_3_out, not_4_out, Op[1], Op[0]);
  and sw (MemWrite, Op[5], not_2_out, Op[3], not_4_out, Op[1], Op[0]);
  and u_ori (ori, not_1_out, not_2_out, Op[3], Op[2], not_5_out, Op[0]);
  and u_j (j, not_1_out, not_2_out, not_3_out, not_4_out, Op[1], not_6_out);
  and u_beq (beq, not_1_out, not_2_out, not_3_out, Op[2], not_5_out, not_6_out);
  and lui (ext_op[1], not_1_out, not_2_out, Op[3], Op[2], Op[1], Op[0]);
  and jal (MemToReg[1], not_1_out, not_2_out, not_3_out, not_4_out, Op[1], Op[0]);
  not not_7 (not_7_out, func[3]);
  not not_8 (not_8_out, func[4]);
  not not_9 (not_9_out, func[5]);
  not not_10 (not_10_out, func[1]);
  not not_11 (not_11_out, func[2]);
  not not_12 (not_12_out, func[0]);
  and u_addu (addu, R, func[5], not_8_out, not_7_out, not_11_out, not_10_out, func[0]);
  and u_subu (subu, R, func[5], not_8_out, not_7_out, not_11_out, func[1], func[0]);
  and u_nop (nop, R, not_9_out, not_8_out, not_7_out, not_11_out, not_10_out, not_12_out);
  and u_jr (jr, R, not_9_out, not_8_out, func[3], not_11_out, not_10_out, not_12_out);
  or or_1 (RegDst[0], addu, subu);
  buf or_2 (RegDst[1], MemToReg[1]);  // OR_Gate
  buf or_3 (ext_op[0], ori);  // OR_Gate
  or or_4 (j_jal, j, MemToReg[1]);
  or or_5 (RegWrite, MemRead, addu, subu, ori, ext_op[1], MemToReg[1]);
  or or_6 (ALUSrc, MemWrite, MemRead, ori, ext_op[1]);
  or or_7 (NPC, j, beq, MemToReg[1], jr);
  or or_8 (ALUOp[0], MemWrite, MemRead, MemToReg[1], addu);
  buf or_9 (ALUOp[1], subu);  // OR_Gate
  or or_10 (ALUOp[2], ext_op[1], addu, MemWrite, MemToReg[1], MemRead, subu);
  buf or_11 (ALUOp[3], ori);  // OR_Gate

  assign MemToReg[0] = MemRead;

  // Other names for the same wires on the sheet: lui = ext_op[1]; lw = MemRead; jal = MemToReg[1]; sw = MemWrite
endmodule

module Instr (
  input  [31:0] Instr,
  output [5:0] Op,
  output [5:0] func,
  output [4:0] Rs,
  output [4:0] Rt,
  output [4:0] Rd,
  output [15:0] imm16,
  output [25:0] Jtarget26
);


  assign func = Instr[5:0];
  assign imm16 = Instr[15:0];
  assign Jtarget26 = Instr[25:0];
  assign Op = Instr[31:26];
  assign Rd = Instr[15:11];
  assign Rs = Instr[25:21];
  assign Rt = Instr[20:16];
endmodule

module NPC (
  input  [31:0] PC,
  input  [31:0] imm32,
  input  equal,
  input  [25:0] Jtarget26,
  input  [31:0] RegData,
  input  [1:0] in_6,
  output [31:0] NPC
);

  wire [31:0] adder_1_out, adder_2_out, multiplexer_1_out, shifter_1_out;

  Shifter #(.width(32)) shifter_1 (.in(imm32), .\dist (5'b00010), .out(shifter_1_out));
  Adder #(.width(32)) adder_1 (.a(PC), .b(shifter_1_out), .out(adder_1_out));  // open: cin, cout
  Adder #(.width(32)) adder_2 (.a(PC), .b(32'h4), .out(adder_2_out));  // open: cin, cout
  Multiplexer #(.width(32), .enable("false")) multiplexer_1 (
    .in0(adder_2_out), .in1(adder_1_out), .out(multiplexer_1_out), .sel(equal));
  Multiplexer #(.select(2), .width(32)) multiplexer_2 (
    .in0(adder_2_out), .in1(multiplexer_1_out), .in2({PC[31:28], Jtarget26, 2'b00}), .in3(RegData),
    .out(NPC), .sel(in_6));  // open: en

  // Notes on the sheet:
  //   equal: pull=up
endmodule

module PC (
  input  in_1,
  input  in_2,
  input  stallF,
  input  [31:0] NPC,
  output [23:0] InstrAddr,
  output [31:0] PC
);

  wire comparator_1_eq, not_1_out;
  wire [31:0] register_1_q, subtractor_1_out;

  not not_1 (not_1_out, stallF);
  Register #(.width(32)) register_1 (.D(NPC), .en(not_1_out), .Q(register_1_q), .clk(in_1), .clr(in_2));
  Comparator #(.width(32)) comparator_1 (.a(register_1_q), .b({32{1'b0}}), .eq(comparator_1_eq));  // open: gt, lt
  Multiplexer #(.width(32), .enable("false")) multiplexer_1 (
    .in0(register_1_q), .in1(32'h3000), .out(PC), .sel(comparator_1_eq));
  Subtractor #(.width(32)) subtractor_1 (
    .a(PC), .b(32'h3000), .out({subtractor_1_out[31:26], InstrAddr, subtractor_1_out[1:0]}));  // open: bin, bout

  // Other names for the same wires on the sheet: Clk = in_1; reset = in_2
endmodule

module extender (
  input  [15:0] in_1,
  input  [1:0] in_2,
  output [31:0] out_3
);

  wire [31:0] bit_extender_1_out, bit_extender_2_out;

  assign bit_extender_1_out = {{16{in_1[15]}}, in_1};  // Bit_Extender bit_extender_1
  assign bit_extender_2_out = {{16{1'b0}}, in_1};  // Bit_Extender bit_extender_2
  Multiplexer #(.select(2), .width(32), .enable("false")) multiplexer_1 (
    .in0(bit_extender_1_out), .in1(bit_extender_2_out), .in2({in_1, {16{1'b0}}}), .out(out_3), .sel(in_2));  // open: in3
endmodule

module DM (
  input  in_1,
  input  in_2,
  input  in_3,
  input  in_4,
  input  [31:0] in_5,
  input  [31:0] in_6,
  output [31:0] out_7
);

  RAM #(.addrWidth(24), .dataWidth(32), .bus("separate")) ram_1 (
    .addr(in_5[25:2]), .din(in_6), .data(out_7), .str(in_3), .clk(in_1), .ld(in_4), .clr(in_2));  // open: sel

  // Other names for the same wires on the sheet: Clk = in_1; MemRead = in_4; MemWrite = in_3; reset = in_2
endmodule

module NPCop (
  input  beq,
  input  j_jal,
  input  jr,
  output [1:0] out_4
);

  or or_1 (out_4[0], jr, beq);
  or or_2 (out_4[1], j_jal, jr);
endmodule

module control2 (
  input  [5:0] Op,
  input  [5:0] func,
  output addu,
  output lw,
  output subu,
  output sw,
  output nop,
  output ori,
  output jr,
  output j,
  output beq,
  output lui,
  output jal
);

  wire not_1_out, not_2_out, not_3_out, not_4_out, not_5_out, not_6_out, not_7_out, not_8_out, not_9_out,
       not_10_out, not_11_out, not_12_out, R;

  not not_1 (not_1_out, Op[5]);
  not not_2 (not_2_out, Op[1]);
  not not_3 (not_3_out, Op[3]);
  not not_4 (not_4_out, Op[2]);
  not not_5 (not_5_out, Op[4]);
  not not_6 (not_6_out, Op[0]);
  and u_R (R, not_1_out, not_5_out, not_3_out, not_4_out, not_2_out, not_6_out);
  and u_lw (lw, Op[5], not_5_out, not_3_out, not_4_out, Op[1], Op[0]);
  and u_sw (sw, Op[5], not_5_out, Op[3], not_4_out, Op[1], Op[0]);
  and u_ori (ori, not_1_out, not_5_out, Op[3], Op[2], not_2_out, Op[0]);
  and u_j (j, not_1_out, not_5_out, not_3_out, not_4_out, Op[1], not_6_out);
  and u_beq (beq, not_1_out, not_5_out, not_3_out, Op[2], not_2_out, not_6_out);
  and u_lui (lui, not_1_out, not_5_out, Op[3], Op[2], Op[1], Op[0]);
  and u_jal (jal, not_1_out, not_5_out, not_3_out, not_4_out, Op[1], Op[0]);
  not not_7 (not_7_out, func[4]);
  not not_8 (not_8_out, func[5]);
  not not_9 (not_9_out, func[3]);
  not not_10 (not_10_out, func[2]);
  not not_11 (not_11_out, func[1]);
  not not_12 (not_12_out, func[0]);
  and u_addu (addu, R, func[5], not_7_out, not_9_out, not_10_out, not_11_out, func[0]);
  and u_subu (subu, R, func[5], not_7_out, not_9_out, not_10_out, func[1], func[0]);
  and u_nop (nop, R, not_8_out, not_7_out, not_9_out, not_10_out, not_11_out, not_12_out);
  and u_jr (jr, R, not_8_out, not_7_out, func[3], not_10_out, not_11_out, not_12_out);

  // Notes on the sheet:
  //   jal: pull=up
  //   jr: pull=up
  //   addu: pull=up
  //   nop: pull=up
  //   subu: pull=up
  //   lui: pull=up
endmodule

module D (
  input  [31:0] Instr,
  output [4:0] S1_D,
  output [4:0] S2_D,
  output [1:0] tuse1_D,
  output [1:0] tuse2_D
);

  wire addu, beq, j, jal, jr, lui, lw, nop, or_1_out, or_2_out, or_3_out, ori, subu, sw;
  wire [1:0] or_4_out;
  wire [4:0] instr_1_rs, instr_1_rt;
  wire [5:0] instr_1_func, instr_1_op;

  control2 control2_1 (
    .addu(addu), .lw(lw), .subu(subu), .sw(sw), .nop(nop), .ori(ori), .jr(jr), .j(j), .beq(beq), .lui(lui),
    .jal(jal), .Op(instr_1_op), .func(instr_1_func));
  Instr instr_1 (
    .Instr(Instr), .func(instr_1_func), .Rs(instr_1_rs), .Rt(instr_1_rt), .Op(instr_1_op));  // open: Rd, imm16, Jtarget26
  or or_1 (or_1_out, lw, sw, ori, beq, addu, subu, jr);
  Multiplexer #(.width(5), .enable("false")) multiplexer_1 (
    .in0({5{1'b0}}), .in1(instr_1_rs), .out(S1_D), .sel(or_1_out));
  or or_2 (or_2_out, sw, beq, addu, subu);
  Multiplexer #(.width(5), .enable("false")) multiplexer_2 (
    .in0({5{1'b0}}), .in1(instr_1_rt), .out(S2_D), .sel(or_2_out));
  or or_3 (or_3_out, lw, sw, ori, addu, subu);
  or or_4 (or_4_out[0], addu, subu);
  buf or_5 (or_4_out[1], sw);  // OR_Gate
  Multiplexer #(.width(2), .enable("false")) multiplexer_3 (.in0(2'b00), .in1(2'b01), .out(tuse1_D), .sel(or_3_out));
  Multiplexer #(.select(2), .width(2), .enable("false")) multiplexer_4 (
    .in0(2'b00), .in1(2'b01), .in2(2'b10), .out(tuse2_D), .sel(or_4_out));  // open: in3
endmodule

module E (
  input  [31:0] Instr,
  input  [31:0] pc_8,
  input  [31:0] imm32,
  output [4:0] S1_E,
  output [4:0] S2_E,
  output [4:0] DES_E,
  output [3:0] tnew_E,
  output [31:0] E__D
);

  wire addu, beq, j, jal, jr, lui, lw, nop, or_1_out, or_8_out, ori, subu, sw;
  wire [1:0] or_2_out, or_4_out, or_6_out;
  wire [4:0] instr_1_rd, instr_1_rs, instr_1_rt;
  wire [5:0] instr_1_func, instr_1_op;

  control2 control2_1 (
    .addu(addu), .lw(lw), .subu(subu), .sw(sw), .nop(nop), .ori(ori), .jr(jr), .j(j), .beq(beq), .lui(lui),
    .jal(jal), .Op(instr_1_op), .func(instr_1_func));
  Instr instr_1 (
    .Instr(Instr), .func(instr_1_func), .Rs(instr_1_rs), .Rt(instr_1_rt), .Rd(instr_1_rd), .Op(instr_1_op));  // open: imm16, Jtarget26
  or or_1 (or_1_out, lw, sw, ori, addu, subu);
  Multiplexer #(.width(5), .enable("false")) multiplexer_1 (
    .in0({5{1'b0}}), .in1(instr_1_rs), .out(S1_E), .sel(or_1_out));
  or or_2 (or_2_out[0], lui, lw, jal, ori);
  or or_3 (or_2_out[1], jal, addu, subu);
  or or_4 (or_4_out[0], lui, addu, subu, ori);
  buf or_5 (or_4_out[1], lw);  // OR_Gate
  buf or_6 (or_6_out[0], jal);  // OR_Gate
  buf or_7 (or_6_out[1], lui);  // OR_Gate
  Multiplexer #(.width(5), .enable("false")) multiplexer_2 (
    .in0({5{1'b0}}), .in1(instr_1_rt), .out(S2_E), .sel(or_8_out));
  or or_8 (or_8_out, sw, addu, subu);
  Multiplexer #(.select(2), .width(5), .enable("false")) multiplexer_3 (
    .in0({5{1'b0}}), .in1(instr_1_rt), .in2(instr_1_rd), .in3({5{1'b1}}), .out(DES_E), .sel(or_2_out));
  Multiplexer #(.select(2), .width(4), .enable("false")) multiplexer_4 (
    .in0(4'b0000), .in1(4'b0001), .in2(4'b0010), .out(tnew_E), .sel(or_4_out));  // open: in3
  Multiplexer #(.select(2), .width(32), .enable("false")) multiplexer_5 (
    .in0({32{1'b0}}), .in1(pc_8), .in2(imm32), .out(E__D), .sel(or_6_out));  // open: in3
endmodule

module M (
  input  [31:0] Instr,
  input  [31:0] pc_8,
  input  [31:0] ALUresult,
  output [4:0] S2_M,
  output [4:0] DES_M,
  output [3:0] tnew_M,
  output [31:0] M__D
);

  wire addu, beq, j, jal, jr, lui, lw, nop, or_5_out, or_6_out, ori, subu, sw;
  wire [1:0] or_1_out, or_3_out;
  wire [4:0] instr_1_rd, instr_1_rt;
  wire [5:0] instr_1_func, instr_1_op;

  control2 control2_1 (
    .addu(addu), .lw(lw), .subu(subu), .sw(sw), .nop(nop), .ori(ori), .jr(jr), .j(j), .beq(beq), .lui(lui),
    .jal(jal), .Op(instr_1_op), .func(instr_1_func));
  Instr instr_1 (
    .Instr(Instr), .func(instr_1_func), .Rt(instr_1_rt), .Rd(instr_1_rd), .Op(instr_1_op));  // open: Rs, imm16, Jtarget26
  or or_1 (or_1_out[0], lui, lw, jal, ori);
  or or_2 (or_1_out[1], jal, addu, subu);
  buf or_3 (or_3_out[0], jal);  // OR_Gate
  or or_4 (or_3_out[1], ori, lui, addu, subu);
  Multiplexer #(.width(5), .enable("false")) multiplexer_1 (
    .in0({5{1'b0}}), .in1(instr_1_rt), .out(S2_M), .sel(or_5_out));
  buf or_5 (or_5_out, sw);  // OR_Gate
  Multiplexer #(.select(2), .width(5), .enable("false")) multiplexer_2 (
    .in0({5{1'b0}}), .in1(instr_1_rt), .in2(instr_1_rd), .in3({5{1'b1}}), .out(DES_M), .sel(or_1_out));
  Multiplexer #(.width(4), .enable("false")) multiplexer_3 (.in0(4'b0000), .in1(4'b0001), .out(tnew_M), .sel(or_6_out));
  buf or_6 (or_6_out, lw);  // OR_Gate
  Multiplexer #(.select(2), .width(32), .enable("false")) multiplexer_4 (
    .in0({32{1'b0}}), .in1(pc_8), .in2(ALUresult), .out(M__D), .sel(or_3_out));  // open: in3
endmodule

module W (
  input  [31:0] Instr,
  input  [31:0] pc_8,
  input  [31:0] ALUresult,
  input  [31:0] readData_W,
  output [4:0] DES_W,
  output [3:0] tnew_W,
  output [31:0] W__D
);

  wire addu, beq, j, jal, jr, lui, lw, nop, ori, subu, sw;
  wire [1:0] or_1_out, or_3_out;
  wire [4:0] instr_1_rd, instr_1_rt;
  wire [5:0] instr_1_func, instr_1_op;

  control2 control2_1 (
    .addu(addu), .lw(lw), .subu(subu), .sw(sw), .nop(nop), .ori(ori), .jr(jr), .j(j), .beq(beq), .lui(lui),
    .jal(jal), .Op(instr_1_op), .func(instr_1_func));
  Instr instr_1 (
    .Instr(Instr), .func(instr_1_func), .Rt(instr_1_rt), .Rd(instr_1_rd), .Op(instr_1_op));  // open: Rs, imm16, Jtarget26
  or or_1 (or_1_out[0], lui, lw, jal, ori);
  or or_2 (or_1_out[1], jal, addu, subu);
  or or_3 (or_3_out[0], lw, jal);
  or or_4 (or_3_out[1], ori, lui, lw, addu, subu);
  Multiplexer #(.select(2), .width(5), .enable("false")) multiplexer_1 (
    .in0({5{1'b0}}), .in1(instr_1_rt), .in2(instr_1_rd), .in3({5{1'b1}}), .out(DES_W), .sel(or_1_out));
  Multiplexer #(.select(2), .width(32), .enable("false")) multiplexer_2 (
    .in0({32{1'b0}}), .in1(pc_8), .in2(ALUresult), .in3(readData_W), .out(W__D), .sel(or_3_out));

  assign tnew_W = 4'b0000;
endmodule
