// Logisim project single_cycle_cpu_hjc-owo.circ as structural Verilog: 7 circuits, main circuit main
module main (
  input  in_1,
  output [31:0] out_2,
  output out_3,
  output [4:0] out_4,
  output [31:0] out_5,
  output out_6,
  output [4:0] out_7,
  output [31:0] out_8
);

  wire ALUSrc, branch, Clk, equal, jump, MemRead, MemToReg, RegDst;
  wire [3:0] ALUOp;
  wire [4:0] Rd, Rs, Rt;
  wire [5:0] func, Op;
  wire [25:0] Jtarget26;
  wire [31:0] alu_1_out_5, grf_1_rd1, imm32, multiplexer_2_out, npc_1_npc, pc_1_out_4, ram_1_data;

  Clock clock_1 (.out(Clk));
  Multiplexer #(.width(5), .enable("false")) multiplexer_1 (.in0(Rt), .in1(Rd), .out(out_4), .sel(RegDst));
  PC pc_1 (.in_1(in_1), .in_2(Clk), .in_3(npc_1_npc), .out_4(pc_1_out_4));
  GRF grf_1 (
    .A1(Rs), .A2(Rt), .A3(out_4), .WD(out_5), .RD1(grf_1_rd1), .RD2(out_8), .clk(Clk), .reset(in_1),
    .we(out_3));
  Multiplexer #(.width(32), .enable("false")) multiplexer_2 (
    .in0(out_8), .in1(imm32), .out(multiplexer_2_out), .sel(ALUSrc));
  Instr instr_1 (.Instr(out_2), .func(func), .Rs(Rs), .Rt(Rt), .Rd(Rd), .Op(Op), .imm32(imm32), .Jtarget26(Jtarget26));
  NPC npc_1 (
    .imm32(imm32), .Jtarget26(Jtarget26), .jump(jump), .equal(equal), .branch(branch), .PC(pc_1_out_4),
    .NPC(npc_1_npc));
  ROM #(.addrWidth(5), .dataWidth(32)) rom_1 (.addr(pc_1_out_4[6:2]), .data(out_2));  // open: sel
  ALU alu_1 (
    .in_1(grf_1_rd1), .in_2(multiplexer_2_out), .equal(equal),
    .out_5({alu_1_out_5[31:7], out_7, alu_1_out_5[1:0]}), .in_3(ALUOp));
  Multiplexer #(.width(32), .enable("false")) multiplexer_3 (
    .in0({alu_1_out_5[31:7], out_7, alu_1_out_5[1:0]}), .in1(ram_1_data), .out(out_5), .sel(MemToReg));
  RAM #(.addrWidth(5), .dataWidth(32), .bus("separate")) ram_1 (
    .addr(out_7), .din(out_8), .data(ram_1_data), .str(out_6), .clk(Clk), .ld(MemRead), .clr(in_1));  // open: sel
  control control_1 (
    .jump(jump), .branch(branch), .MemToReg(MemToReg), .MemWrite(out_6), .MemRead(MemRead), .ALUSrc(ALUSrc),
    .RegWrite(out_3), .RegDst(RegDst), .ALUOp(ALUOp), .Op(Op), .func(func));

  // Other names for the same wires on the sheet: MemAddr[4:0] = out_7; Instr[31:0] = out_2; MemData[31:0] = out_8;
  //   MemWrite = out_6; RegAddr[4:0] = out_4; RegData[31:0] = out_5; RegWrite = out_3; reset = in_1
endmodule

module GRF (
  input  [4:0] A1,
  input  clk,
  input  reset,
  input  we,
  input  [4:0] A2,
  input  [4:0] A3,
  input  [31:0] WD,
  output [31:0] RD1,
  output [31:0] RD2
);

  wire [31:0] I0, I1, I2, I3, I4, I5, I6, I7, I8, I9, I10, I11, I12, I13, I14, I15, I16, I17, I18, I19, I20,
       I21, I22, I23, I24, I25, I26, I27, I28, I29, I30, I31, O0, O1, O2, O3, O4, O5, O6, O7, O8, O9, O10,
       O11, O12, O13, O14, O15, O16, O17, O18, O19, O20, O21, O22, O23, O24, O25, O26, O27, O28, O29, O30,
       O31;

  Demultiplexer #(.select(5), .width(32), .tristate("true")) demultiplexer_1 (
    .out0(I0), .out1(I1), .out2(I2), .out3(I3), .out4(I4), .out5(I5), .out6(I6), .out7(I7), .out8(I8),
    .out9(I9), .out10(I10), .out11(I11), .out12(I12), .out13(I13), .out14(I14), .out15(I15), .out16(I16),
    .out17(I17), .out18(I18), .out19(I19), .out20(I20), .out21(I21), .out22(I22), .out23(I23), .out24(I24),
    .out25(I25), .out26(I26), .out27(I27), .out28(I28), .out29(I29), .out30(I30), .out31(I31), .in(WD),
    .sel(A3));  // open: en
  Multiplexer #(.select(5), .width(32)) multiplexer_1 (
    .in0(O0), .in1(O1), .in2(O2), .in3(O3), .in4(O4), .in5(O5), .in6(O6), .in7(O7), .in8(O8), .in9(O9),
    .in10(O10), .in11(O11), .in12(O12), .in13(O13), .in14(O14), .in15(O15), .in16(O16), .in17(O17),
    .in18(O18), .in19(O19), .in20(O20), .in21(O21), .in22(O22), .in23(O23), .in24(O24), .in25(O25),
    .in26(O26), .in27(O27), .in28(O28), .in29(O29), .in30(O30), .in31(O31), .out(RD2), .sel(A2));  // open: en
  Multiplexer #(.select(5), .width(32)) multiplexer_2 (
    .in0(O0), .in1(O1), .in2(O2), .in3(O3), .in4(O4), .in5(O5), .in6(O6), .in7(O7), .in8(O8), .in9(O9),
    .in10(O10), .in11(O11), .in12(O12), .in13(O13), .in14(O14), .in15(O15), .in16(O16), .in17(O17),
    .in18(O18), .in19(O19), .in20(O20), .in21(O21), .in22(O22), .in23(O23), .in24(O24), .in25(O25),
    .in26(O26), .in27(O27), .in28(O28), .in29(O29), .in30(O30), .in31(O31), .out(RD1), .sel(A1));  // open: en
  Register #(.width(32)) register_1 (.D({32{1'b0}}), .en(we), .Q(O0), .clk(clk), .clr(reset));
  Register #(.width(32)) register_2 (.D(I8), .en(we), .Q(O8), .clk(clk), .clr(reset));
  Register #(.width(32)) register_3 (.D(I16), .en(we), .Q(O16), .clk(clk), .clr(reset));
  Register #(.width(32)) register_4 (.D(I24), .en(we), .Q(O24), .clk(clk), .clr(reset));
  Register #(.width(32)) register_5 (.D(I1), .en(we), .Q(O1), .clk(clk), .clr(reset));
  Register #(.width(32)) register_6 (.D(I9), .en(we), .Q(O9), .clk(clk), .clr(reset));
  Register #(.width(32)) register_7 (.D(I17), .en(we), .Q(O17), .clk(clk), .clr(reset));
  Register #(.width(32)) register_8 (.D(I25), .en(we), .Q(O25), .clk(clk), .clr(reset));
  Register #(.width(32)) register_9 (.D(I2), .en(we), .Q(O2), .clk(clk), .clr(reset));
  Register #(.width(32)) register_10 (.D(I10), .en(we), .Q(O10), .clk(clk), .clr(reset));
  Register #(.width(32)) register_11 (.D(I18), .en(we), .Q(O18), .clk(clk), .clr(reset));
  Register #(.width(32)) register_12 (.D(I26), .en(we), .Q(O26), .clk(clk), .clr(reset));
  Register #(.width(32)) register_13 (.D(I3), .en(we), .Q(O3), .clk(clk), .clr(reset));
  Register #(.width(32)) register_14 (.D(I11), .en(we), .Q(O11), .clk(clk), .clr(reset));
  Register #(.width(32)) register_15 (.D(I19), .en(we), .Q(O19), .clk(clk), .clr(reset));
  Register #(.width(32)) register_16 (.D(I27), .en(we), .Q(O27), .clk(clk), .clr(reset));
  Register #(.width(32)) register_17 (.D(I4), .en(we), .Q(O4), .clk(clk), .clr(reset));
  Register #(.width(32)) register_18 (.D(I12), .en(we), .Q(O12), .clk(clk), .clr(reset));
  Register #(.width(32)) register_19 (.D(I20), .en(we), .Q(O20), .clk(clk), .clr(reset));
  Register #(.width(32)) register_20 (.D(I28), .en(we), .Q(O28), .clk(clk), .clr(reset));
  Register #(.width(32)) register_21 (.D(I5), .en(we), .Q(O5), .clk(clk), .clr(reset));
  Register #(.width(32)) register_22 (.D(I13), .en(we), .Q(O13), .clk(clk), .clr(reset));
  Register #(.width(32)) register_23 (.D(I21), .en(we), .Q(O21), .clk(clk), .clr(reset));
  Register #(.width(32)) register_24 (.D(I29), .en(we), .Q(O29), .clk(clk), .clr(reset));
  Register #(.width(32)) register_25 (.D(I6), .en(we), .Q(O6), .clk(clk), .clr(reset));
  Register #(.width(32)) register_26 (.D(I14), .en(we), .Q(O14), .clk(clk), .clr(reset));
  Register #(.width(32)) register_27 (.D(I22), .en(we), .Q(O22), .clk(clk), .clr(reset));
  Register #(.width(32)) register_28 (.D(I30), .en(we), .Q(O30), .clk(clk), .clr(reset));
  Register #(.width(32)) register_29 (.D(I7), .en(we), .Q(O7), .clk(clk), .clr(reset));
  Register #(.width(32)) register_30 (.D(I15), .en(we), .Q(O15), .clk(clk), .clr(reset));
  Register #(.width(32)) register_31 (.D(I23), .en(we), .Q(O23), .clk(clk), .clr(reset));
  Register #(.width(32)) register_32 (.D(I31), .en(we), .Q(O31), .clk(clk), .clr(reset));
endmodule

module ALU (
  input  [31:0] in_1,
  input  [31:0] in_2,
  input  [3:0] in_3,
  output equal,
  output [31:0] out_5
);

  wire comparator_1_lt, comparator_2_lt;
  wire [31:0] adder_1_out, and_1_out, bit_extender_1_out, bit_extender_2_out, bit_extender_3_out,
       divider_1_out, multiplier_1_out, nor_1_out, or_1_out, shifter_1_out, shifter_2_out, shifter_3_out,
       shifter_4_out, subtractor_1_out, xor_1_out;

  assign bit_extender_1_out = {{16{1'b0}}, in_2[15:0]};  // Bit_Extender bit_extender_1
  Shifter #(.width(32)) shifter_1 (.in(in_1), .\dist (in_2[4:0]), .out(shifter_1_out));
  Shifter #(.width(32), .shift("ar")) shifter_2 (.in(in_1), .\dist (in_2[4:0]), .out(shifter_2_out));
  Shifter #(.width(32), .shift("lr")) shifter_3 (.in(in_1), .\dist (in_2[4:0]), .out(shifter_3_out));
  Multiplier #(.width(32)) multiplier_1 (.a(in_1), .b(in_2), .out(multiplier_1_out));  // open: cin, cout
  Divider #(.width(32)) divider_1 (.a(in_1), .b(in_2), .out(divider_1_out));  // open: upper, rem
  Adder #(.width(32)) adder_1 (.a(in_1), .b(in_2), .out(adder_1_out));  // open: cin, cout
  Subtractor #(.width(32)) subtractor_1 (.a(in_1), .b(in_2), .out(subtractor_1_out));  // open: bin, bout
  assign and_1_out = in_1 & in_2;  // AND_Gate and_1, 32 bits wide
  assign or_1_out = in_1 | bit_extender_1_out;  // OR_Gate or_1, 32 bits wide
  assign xor_1_out = in_1 ^ in_2;  // XOR_Gate xor_1, 32 bits wide
  assign nor_1_out = ~(in_1 | in_2);  // NOR_Gate nor_1, 32 bits wide
  Comparator #(.width(32)) comparator_1 (.a(in_1), .b(in_2), .lt(comparator_1_lt));  // open: gt, eq
  Comparator #(.width(32), .mode("unsigned")) comparator_2 (.a(in_1), .b(in_2), .lt(comparator_2_lt));  // open: gt, eq
  Shifter #(.width(32)) shifter_4 (.in(in_1), .\dist (5'b10000), .out(shifter_4_out));
  assign bit_extender_2_out = {{31{1'b0}}, comparator_1_lt};  // Bit_Extender bit_extender_2
  assign bit_extender_3_out = {{31{1'b0}}, comparator_2_lt};  // Bit_Extender bit_extender_3
  Comparator #(.width(32)) comparator_3 (.a(subtractor_1_out), .b({32{1'b0}}), .eq(equal));  // open: gt, lt
  Multiplexer #(.select(4), .width(32)) multiplexer_1 (
    .in0(shifter_1_out), .in1(shifter_2_out), .in2(shifter_3_out), .in3(multiplier_1_out),
    .in4(divider_1_out), .in5(adder_1_out), .in6(subtractor_1_out), .in7(and_1_out), .in8(or_1_out),
    .in9(xor_1_out), .in10(nor_1_out), .in11(bit_extender_2_out), .in12(bit_extender_3_out),
    .in13(shifter_4_out), .out(out_5), .sel(in_3));  // open: in14, in15, en
endmodule

module control (
  input  [5:0] Op,
  input  [5:0] func,
  output jump,
  output branch,
  output MemToReg,
  output MemWrite,
  output MemRead,
  output ALUSrc,
  output RegWrite,
  output RegDst,
  output [3:0] ALUOp
);

  wire addu, lui, not_1_out, not_2_out, not_3_out, not_4_out, not_5_out, not_6_out, not_7_out, not_8_out,
       not_9_out, not_10_out, not_11_out, not_12_out, ori, subu;

  not not_1 (not_1_out, Op[5]);
  not not_2 (not_2_out, Op[3]);
  not not_3 (not_3_out, Op[1]);
  not not_4 (not_4_out, Op[4]);
  not not_5 (not_5_out, Op[2]);
  not not_6 (not_6_out, Op[0]);
  and R (RegDst, not_1_out, not_4_out, not_2_out, not_5_out, not_3_out, not_6_out);
  and lw (MemRead, Op[5], not_4_out, not_2_out, not_5_out, Op[1], Op[0]);
  and sw (MemWrite, Op[5], not_4_out, Op[3], not_5_out, Op[1], Op[0]);
  and u_ori (ori, not_1_out, not_4_out, Op[3], Op[2], not_3_out, Op[0]);
  and j (jump, not_1_out, not_4_out, not_2_out, not_5_out, Op[1], not_6_out);
  and beq (branch, not_1_out, not_4_out, not_2_out, Op[2], not_3_out, not_6_out);
  and u_lui (lui, not_1_out, not_4_out, Op[3], Op[2], Op[1], Op[0]);
  not not_7 (not_7_out, func[5]);
  not not_8 (not_8_out, func[3]);
  not not_9 (not_9_out, func[4]);
  not not_10 (not_10_out, func[0]);
  not not_11 (not_11_out, func[1]);
  not not_12 (not_12_out, func[2]);
  and u_addu (addu, RegDst, func[5], not_9_out, not_8_out, not_12_out, not_11_out, func[0]);
  and u_subu (subu, RegDst, func[5], not_9_out, not_8_out, not_12_out, func[1], func[0]);
  or or_1 (ALUSrc, MemWrite, MemRead, ori, lui);
  or or_2 (ALUOp[0], MemWrite, MemRead, addu, lui);
  buf or_3 (ALUOp[1], subu);  // OR_Gate
  or or_4 (ALUOp[2], lui, addu, MemWrite, MemRead, subu);
  or or_5 (ALUOp[3], lui, ori);
  or or_6 (RegWrite, RegDst, ori, MemRead, lui);

  assign MemToReg = MemRead;

  // Other names for the same wires on the sheet: beq = branch; j = jump; lw = MemRead; R = RegDst; sw = MemWrite
endmodule

module Instr (
  input  [31:0] Instr,
  output [5:0] func,
  output [4:0] Rs,
  output [4:0] Rt,
  output [4:0] Rd,
  output [5:0] Op,
  output [31:0] imm32,
  output [25:0] Jtarget26
);

  assign imm32 = {{16{Instr[15]}}, Instr[15:0]};  // Bit_Extender bit_extender_1

  assign func = Instr[5:0];
  assign Jtarget26 = Instr[25:0];
  assign Op = Instr[31:26];
  assign Rd = Instr[15:11];
  assign Rs = Instr[25:21];
  assign Rt = Instr[20:16];
endmodule

module NPC (
  input  [31:0] PC,
  input  [31:0] imm32,
  input  [25:0] Jtarget26,
  input  jump,
  input  equal,
  input  branch,
  output [31:0] NPC
);

  wire and_1_out;
  wire [1:0] or_1_out;
  wire [31:0] adder_1_out, adder_2_out, shifter_1_out;

  Adder #(.width(32)) adder_1 (.a(PC), .b(32'h4), .out(adder_1_out));  // open: cin, cout
  Shifter #(.width(32)) shifter_1 (.in(imm32), .\dist (5'b00010), .out(shifter_1_out));
  and and_1 (and_1_out, equal, branch);
  Adder #(.width(32)) adder_2 (.a(adder_1_out), .b(shifter_1_out), .out(adder_2_out));  // open: cin, cout
  Multiplexer #(.select(2), .width(32)) multiplexer_1 (
    .in0(adder_1_out), .in2(adder_2_out), .in3({adder_1_out[31:28], Jtarget26, 2'b00}), .out(NPC),
    .sel(or_1_out));  // open: in1, en
  buf or_1 (or_1_out[0], jump);  // OR_Gate
  or or_2 (or_1_out[1], jump, and_1_out);
endmodule

module PC (
  input  in_1,
  input  in_2,
  input  [31:0] in_3,
  output [31:0] out_4
);

  wire [31:0] register_1_q, subtractor_1_out;

  Subtractor #(.width(32)) subtractor_1 (.a(in_3), .b(32'h3000), .out(subtractor_1_out));  // open: bin, bout
  Register #(.width(32)) register_1 (.D(subtractor_1_out), .Q(register_1_q), .clk(in_2), .clr(in_1));  // open: en
  Adder #(.width(32)) adder_1 (.a(32'h3000), .b(register_1_q), .out(out_4));  // open: cin, cout

  // Other names for the same wires on the sheet: Clk = in_2; reset = in_1
endmodule
