// Logisim project test3.circ as structural Verilog: 3 circuits, main circuit 2nmod5
module _2nmod5 (
  input  in_1,
  output [2:0] out_2
);

  wire clock_1_out;
  wire [1:0] change_1_out_3, register_1_q;

  Register #(.width(2)) register_1 (.D(change_1_out_3), .Q(register_1_q), .clk(clock_1_out));  // open: en, clr
  change change_1 (.in_1(register_1_q), .in(in_1), .out_3(change_1_out_3));
  Clock clock_1 (.out(clock_1_out));
  \output  output_1 (.in_1(register_1_q), .in(in_1), .out_3(out_2));
endmodule

module change (
  input  [1:0] in_1,
  input  in,
  output [1:0] out_3
);


  assign out_3 = {in_1[0], in};
endmodule

module \output  (
  input  [1:0] in_1,
  input  in,
  output [2:0] out_3
);

  wire and_2_out, and_3_out, not_1_out, not_2_out, not_3_out;

  not not_1 (not_1_out, in);
  not not_2 (not_2_out, in_1[0]);
  not not_3 (not_3_out, in);
  and and_1 (out_3[2], in_1[0], not_1_out);
  and and_2 (and_2_out, not_2_out, not_3_out);
  and and_3 (and_3_out, in_1[0], in);
  or or_1 (out_3[0], and_2_out, and_3_out);

  assign out_3[1] = in;
endmodule
