// Logisim project test4.circ as structural Verilog: 1 circuit, main circuit check
module check (
  input  [8:0] in_1,
  output [7:0] out_2
);

  wire not_1_out, xor_1_out, xor_2_out, xor_3_out, xor_4_out, xor_5_out, xor_6_out, xor_7_out, xor_8_out;

  not not_1 (not_1_out, in_1[0]);
  xor xor_1 (xor_1_out, in_1[1], in_1[2]);
  xor xor_2 (xor_2_out, xor_1_out, in_1[3]);
  xor xor_3 (xor_3_out, xor_2_out, in_1[4]);
  xor xor_4 (xor_4_out, xor_3_out, in_1[5]);
  xor xor_5 (xor_5_out, xor_4_out, in_1[6]);
  xor xor_6 (xor_6_out, xor_5_out, in_1[7]);
  xor xor_7 (xor_7_out, xor_6_out, in_1[8]);
  Multiplexer #(.width(8)) multiplexer_1 (.in0({8{1'b1}}), .in1(in_1[8:1]), .out(out_2), .sel(xor_8_out));  // open: en
  xor xor_8 (xor_8_out, not_1_out, xor_7_out);
endmodule
