// Logisim project test5.circ as structural Verilog: 2 circuits, main circuit sort
module sort (
  input  [3:0] in_1,
  input  [3:0] in_2,
  input  [3:0] in_3,
  input  [3:0] in_4,
  output [3:0] out_5,
  output [3:0] out_6,
  output [3:0] out_7,
  output [3:0] out_8
);

  wire [3:0] cmp_1_out_3, cmp_1_out_4, cmp_2_out_3, cmp_2_out_4, cmp_3_out_4, cmp_4_out_3;

  cmp cmp_1 (.in_1(in_1), .in_2(in_2), .out_3(cmp_1_out_3), .out_4(cmp_1_out_4));
  cmp cmp_2 (.in_1(in_3), .in_2(in_4), .out_3(cmp_2_out_3), .out_4(cmp_2_out_4));
  cmp cmp_3 (.in_1(cmp_1_out_3), .in_2(cmp_2_out_3), .out_3(out_5), .out_4(cmp_3_out_4));
  cmp cmp_4 (.in_1(cmp_1_out_4), .in_2(cmp_2_out_4), .out_3(cmp_4_out_3), .out_4(out_8));
  cmp cmp_5 (.in_1(cmp_3_out_4), .in_2(cmp_4_out_3), .out_3(out_6), .out_4(out_7));
endmodule

module cmp (
  input  [3:0] in_1,
  input  [3:0] in_2,
  output [3:0] out_3,
  output [3:0] out_4
);

  wire comparator_1_eq, comparator_1_gt, comparator_2_lt, or_1_out;

  Comparator #(.width(4), .mode("unsigned")) comparator_1 (
    .a(in_1), .b(in_2), .gt(comparator_1_gt), .eq(comparator_1_eq));  // open: lt
  Comparator #(.width(4), .mode("unsigned")) comparator_2 (.a(in_1), .b(in_2), .lt(comparator_2_lt));  // open: gt, eq
  or or_1 (or_1_out, comparator_1_gt, comparator_1_eq);
  Multiplexer #(.width(4)) multiplexer_1 (.in0(in_2), .in1(in_1), .out(out_3), .sel(or_1_out));  // open: en
  Multiplexer #(.width(4)) multiplexer_2 (.in0(in_2), .in1(in_1), .out(out_4), .sel(comparator_2_lt));  // open: en
endmodule
