// Logisim project vote0.circ as structural Verilog
module vote0 (
  input  a1,
  input  a2,
  input  a3,
  input  a4,
  input  a5,
  output \output 
);

  wire and_1_out, and_2_out, and_3_out, and_4_out, and_5_out, and_6_out, and_7_out, and_8_out, and_9_out,
       and_10_out;

  and and_1 (and_1_out, a3, a4, a5);
  and and_2 (and_2_out, a2, a4, a5);
  and and_3 (and_3_out, a2, a3, a5);
  and and_4 (and_4_out, a2, a3, a4);
  and and_5 (and_5_out, a1, a4, a5);
  and and_6 (and_6_out, a1, a3, a5);
  and and_7 (and_7_out, a1, a3, a4);
  and and_8 (and_8_out, a1, a2, a5);
  and and_9 (and_9_out, a1, a2, a4);
  and and_10 (and_10_out, a1, a2, a3);
  or or_1 (\output , and_1_out, and_2_out, and_3_out, and_4_out, and_5_out, and_6_out, and_7_out, and_8_out, and_9_out, and_10_out);
endmodule
